// Logisim project ALU.circ as structural Verilog: 11 circuits, main circuit main
module main (
  input  in_1,
  input  in_2,
  input  in_3,
  input  in_4,
  input  in_5,
  input  in_6,
  input  in_7,
  input  in_8,
  input  in_9,
  input  in_10,
  input  in_11,
  input  in_12,
  input  in_13,
  input  in_14,
  input  in_15,
  output [7:0] out_16,
  output [2:0] out_17
);

  wire clock_1_out;
  wire [2:0] alu_1_overflow;
  wire [7:0] alu_1_out_9, n4_combinator_1_out_9, register_1_out_5, register_2_out_5, register_3_out_5,
       register_4_out_5, register_5_out_5;

  Clock clock_1 (.out(clock_1_out));
  register register_1 (
    .CLK(clock_1_out), .R_W(in_5), .ENABLE(in_8), .INPUT(n4_combinator_1_out_9), .out_5(register_1_out_5));
  register register_2 (
    .CLK(clock_1_out), .R_W(in_12), .ENABLE(in_13), .INPUT(n4_combinator_1_out_9), .out_5(register_2_out_5));
  _3_Combinator u_3_combinator_1 (
    .in_2(register_1_out_5), .in_4(register_2_out_5), .in_6(register_4_out_5), .out_7(out_16), .in_1(in_8),
    .in_3(in_13), .in_5(in_14));
  StatusRegister statusregister_1 (
    .CLK(clock_1_out), .R_W(in_6), .ENABLE(in_7), .INPUT(alu_1_overflow), .out_5(out_17));
  register register_3 (
    .CLK(clock_1_out), .R_W(in_2), .ENABLE(in_1), .INPUT(n4_combinator_1_out_9), .out_5(register_3_out_5));
  register register_4 (.CLK(clock_1_out), .R_W(in_15), .ENABLE(in_14), .INPUT(alu_1_out_9), .out_5(register_4_out_5));
  register register_5 (
    .CLK(clock_1_out), .R_W(in_4), .ENABLE(in_3), .INPUT(n4_combinator_1_out_9), .out_5(register_5_out_5));
  ALU alu_1 (
    .in_3(register_5_out_5), .in_4(register_3_out_5), .in_5(in_11), .in_2(in_9), .in_1(in_10),
    .Overflow(alu_1_overflow[0]), .Zero(alu_1_overflow[1]), .Negative(alu_1_overflow[2]), .out_9(alu_1_out_9));
  _4_combinator u_4_combinator_1 (
    .in_2(out_16), .in_4(out_16), .in_6(out_16), .in_8(out_16), .out_9(n4_combinator_1_out_9), .in_1(in_8),
    .in_3(in_13), .in_5(in_3), .in_7(in_1));

  // Notes on the sheet:
  //   CPU BUS
  //   D0
  //   D1
  //   L Register
  //   3 register can output can leave the CPU bus region to somwhere else.
  //   4 registers can be sent input through the CPU bus
  //   A out
  //   R Register
endmodule

module register (
  input  CLK,
  input  R_W,
  input  ENABLE,
  input  [7:0] INPUT,
  output [7:0] out_5
);

  wire and_1_out, and_2_out, and_3_out, and_4_out, and_5_out, and_6_out, and_7_out, and_8_out, and_9_out,
       and_10_out, not_1_out, not_2_out, not_3_out, not_4_out, not_5_out, not_6_out, not_7_out, not_8_out,
       not_9_out, s_r_ff_1_q, s_r_ff_2_q, s_r_ff_3_q, s_r_ff_4_q, s_r_ff_5_q, s_r_ff_6_q, s_r_ff_7_q,
       s_r_ff_8_q;

  and and_1 (and_1_out, CLK, ENABLE);
  and and_2 (and_2_out, CLK, R_W, ENABLE);
  and and_3 (and_3_out, INPUT[0], CLK, R_W);
  not not_1 (not_1_out, and_3_out);
  and and_4 (and_4_out, INPUT[1], CLK, R_W);
  not not_2 (not_2_out, and_4_out);
  and and_5 (and_5_out, INPUT[2], CLK, R_W);
  not not_3 (not_3_out, and_5_out);
  and and_6 (and_6_out, INPUT[3], CLK, R_W);
  not not_4 (not_4_out, and_6_out);
  and and_7 (and_7_out, INPUT[4], CLK, R_W);
  not not_5 (not_5_out, and_7_out);
  and and_8 (and_8_out, INPUT[5], CLK, R_W);
  not not_6 (not_6_out, and_8_out);
  and and_9 (and_9_out, INPUT[6], CLK, R_W);
  not not_7 (not_7_out, and_9_out);
  and and_10 (and_10_out, INPUT[7], CLK, R_W);
  not not_8 (not_8_out, and_10_out);
  not not_9 (not_9_out, R_W);
  S_R_Flip_Flop #(.trigger("high")) s_r_ff_1 (
    .S(and_3_out), .clk(and_2_out), .R(not_1_out), .Q(s_r_ff_1_q));  // open: Qn, preset, reset, en
  S_R_Flip_Flop #(.trigger("high")) s_r_ff_2 (
    .S(and_4_out), .clk(and_2_out), .R(not_2_out), .Q(s_r_ff_2_q));  // open: Qn, preset, reset, en
  S_R_Flip_Flop #(.trigger("high")) s_r_ff_3 (
    .S(and_5_out), .clk(and_2_out), .R(not_3_out), .Q(s_r_ff_3_q));  // open: Qn, preset, reset, en
  S_R_Flip_Flop #(.trigger("high")) s_r_ff_4 (
    .S(and_6_out), .clk(and_2_out), .R(not_4_out), .Q(s_r_ff_4_q));  // open: Qn, preset, reset, en
  S_R_Flip_Flop #(.trigger("high")) s_r_ff_5 (
    .S(and_7_out), .clk(and_2_out), .R(not_5_out), .Q(s_r_ff_5_q));  // open: Qn, preset, reset, en
  S_R_Flip_Flop #(.trigger("high")) s_r_ff_6 (
    .S(and_8_out), .clk(and_2_out), .R(not_6_out), .Q(s_r_ff_6_q));  // open: Qn, preset, reset, en
  S_R_Flip_Flop #(.trigger("high")) s_r_ff_7 (
    .S(and_9_out), .clk(and_2_out), .R(not_7_out), .Q(s_r_ff_7_q));  // open: Qn, preset, reset, en
  S_R_Flip_Flop #(.trigger("high")) s_r_ff_8 (
    .S(and_10_out), .clk(and_2_out), .R(not_8_out), .Q(s_r_ff_8_q));  // open: Qn, preset, reset, en
  and and_11 (out_5[0], s_r_ff_1_q, and_1_out, not_9_out);
  and and_12 (out_5[1], s_r_ff_2_q, and_1_out, not_9_out);
  and and_13 (out_5[2], s_r_ff_3_q, and_1_out, not_9_out);
  and and_14 (out_5[3], s_r_ff_4_q, and_1_out, not_9_out);
  and and_15 (out_5[4], s_r_ff_5_q, and_1_out, not_9_out);
  and and_16 (out_5[5], s_r_ff_6_q, and_1_out, not_9_out);
  and and_17 (out_5[6], s_r_ff_7_q, and_1_out, not_9_out);
  and and_18 (out_5[7], s_r_ff_8_q, and_1_out, not_9_out);
endmodule

module ALU (
  input  in_1,
  input  in_2,
  input  [7:0] in_3,
  input  [7:0] in_4,
  input  in_5,
  output Overflow,
  output Zero,
  output Negative,
  output [7:0] out_9
);

  wire and_1_out, and_2_out, and_3_out, and_4_out, and_5_out, and_6_out, and_7_out, and_8_out, and_17_out,
       and_18_out, and_19_out, and_20_out, and_21_out, and_22_out, and_23_out, and_24_out, and_25_out,
       and_26_out, and_27_out, and_28_out, and_29_out, and_30_out, and_31_out, and_32_out,
       full_adder_1_out_4, full_adder_1_out_5, full_adder_2_out_4, full_adder_2_out_5, full_adder_3_out_4,
       full_adder_3_out_5, full_adder_4_out_4, full_adder_4_out_5, full_adder_5_out_4, full_adder_5_out_5,
       full_adder_6_out_4, full_adder_6_out_5, full_adder_7_out_4, full_adder_7_out_5, half_adder_1_out_3,
       half_adder_1_out_4, not_1_out, not_2_out, not_3_out, not_4_out, not_5_out, not_6_out, not_7_out,
       not_8_out, not_9_out, or_1_out, or_3_out, xor_1_out;
  wire [7:0] alu2c_1_out_3, and_9_out;
  wire [15:0] adder_1_out, adder_2_out, adder_3_out, adder_4_out, adder_5_out, adder_6_out, adder_7_out,
       adder_8_out, multhelper_1_out_3, multhelper_2_out_3, multhelper_3_out_3, multhelper_4_out_3,
       multhelper_5_out_3, multhelper_6_out_3, multhelper_7_out_3, multhelper_8_out_3, n16bitshift_1_out_2,
       n16bitshift_2_out_2, n16bitshift_3_out_2, n16bitshift_4_out_2, n16bitshift_5_out_2,
       n16bitshift_6_out_2, n16bitshift_7_out_2, n16bitshift_8_out_2, n16bitshift_9_out_2,
       n16bitshift_10_out_2, n16bitshift_11_out_2, n16bitshift_12_out_2, n16bitshift_13_out_2,
       n16bitshift_14_out_2, n16bitshift_15_out_2, n16bitshift_16_out_2, n16bitshift_17_out_2,
       n16bitshift_18_out_2, n16bitshift_19_out_2, n16bitshift_20_out_2, n16bitshift_21_out_2,
       n16bitshift_22_out_2, n16bitshift_23_out_2, n16bitshift_24_out_2, n16bitshift_25_out_2,
       n16bitshift_26_out_2, n16bitshift_27_out_2, n16bitshift_28_out_2;

  and and_1 (and_1_out, in_3[0], in_5);
  and and_2 (and_2_out, in_3[1], in_5);
  and and_3 (and_3_out, in_3[2], in_5);
  and and_4 (and_4_out, in_3[3], in_5);
  and and_5 (and_5_out, in_3[4], in_5);
  and and_6 (and_6_out, in_3[5], in_5);
  and and_7 (and_7_out, in_3[6], in_5);
  and and_8 (and_8_out, in_3[7], in_5);
  and and_9 (and_9_out[0], in_4[0], in_5);
  and and_10 (and_9_out[1], in_4[1], in_5);
  and and_11 (and_9_out[2], in_4[2], in_5);
  and and_12 (and_9_out[3], in_4[3], in_5);
  and and_13 (and_9_out[4], in_4[4], in_5);
  and and_14 (and_9_out[5], in_4[5], in_5);
  and and_15 (and_9_out[6], in_4[6], in_5);
  and and_16 (and_9_out[7], in_4[7], in_5);
  ALU2C alu2c_1 (.in_1(in_2), .in_2(in_4), .out_3(alu2c_1_out_3));
  or or_1 (or_1_out, in_1, in_2);
  multhelper multhelper_1 (.in_1({{8{1'b0}}, and_9_out}), .out_3(multhelper_1_out_3), .in_2(and_1_out));
  and and_17 (and_17_out, in_3[0], or_1_out);
  and and_18 (and_18_out, in_3[1], or_1_out);
  and and_19 (and_19_out, in_3[2], or_1_out);
  and and_20 (and_20_out, in_3[3], or_1_out);
  and and_21 (and_21_out, in_3[4], or_1_out);
  and and_22 (and_22_out, in_3[5], or_1_out);
  and and_23 (and_23_out, in_3[6], or_1_out);
  and and_24 (and_24_out, in_3[7], or_1_out);
  and and_25 (and_25_out, alu2c_1_out_3[0], or_1_out);
  and and_26 (and_26_out, alu2c_1_out_3[1], or_1_out);
  and and_27 (and_27_out, alu2c_1_out_3[2], or_1_out);
  and and_28 (and_28_out, alu2c_1_out_3[3], or_1_out);
  and and_29 (and_29_out, alu2c_1_out_3[4], or_1_out);
  and and_30 (and_30_out, alu2c_1_out_3[5], or_1_out);
  and and_31 (and_31_out, alu2c_1_out_3[6], or_1_out);
  and and_32 (and_32_out, alu2c_1_out_3[7], or_1_out);
  Adder #(.width(16)) adder_1 (.a(multhelper_1_out_3), .b({16{1'b0}}), .out(adder_1_out));  // open: cin, cout
  multhelper multhelper_2 (.in_1({{8{1'b0}}, and_9_out}), .out_3(multhelper_2_out_3), .in_2(and_2_out));
  _16bitshift u_16bitshift_1 (.in_1(multhelper_2_out_3), .out_2(n16bitshift_1_out_2));
  Adder #(.width(16)) adder_2 (.a(n16bitshift_1_out_2), .b(adder_1_out), .out(adder_2_out));  // open: cin, cout
  multhelper multhelper_3 (.in_1({{8{1'b0}}, and_9_out}), .out_3(multhelper_3_out_3), .in_2(and_3_out));
  _16bitshift u_16bitshift_2 (.in_1(multhelper_3_out_3), .out_2(n16bitshift_2_out_2));
  _16bitshift u_16bitshift_3 (.in_1(n16bitshift_2_out_2), .out_2(n16bitshift_3_out_2));
  Adder #(.width(16)) adder_3 (.a(n16bitshift_3_out_2), .b(adder_2_out), .out(adder_3_out));  // open: cin, cout
  multhelper multhelper_4 (.in_1({{8{1'b0}}, and_9_out}), .out_3(multhelper_4_out_3), .in_2(and_4_out));
  _16bitshift u_16bitshift_4 (.in_1(multhelper_4_out_3), .out_2(n16bitshift_4_out_2));
  _16bitshift u_16bitshift_5 (.in_1(n16bitshift_4_out_2), .out_2(n16bitshift_5_out_2));
  _16bitshift u_16bitshift_6 (.in_1(n16bitshift_5_out_2), .out_2(n16bitshift_6_out_2));
  Adder #(.width(16)) adder_4 (.a(n16bitshift_6_out_2), .b(adder_3_out), .out(adder_4_out));  // open: cin, cout
  half_adder half_adder_1 (
    .in_1(and_17_out), .in_2(and_25_out), .out_3(half_adder_1_out_3), .out_4(half_adder_1_out_4));
  full_adder full_adder_1 (
    .in_2(and_18_out), .in_3(and_26_out), .out_4(full_adder_1_out_4), .in_1(half_adder_1_out_4),
    .out_5(full_adder_1_out_5));
  full_adder full_adder_2 (
    .in_2(and_19_out), .in_3(and_27_out), .out_4(full_adder_2_out_4), .in_1(full_adder_1_out_5),
    .out_5(full_adder_2_out_5));
  full_adder full_adder_3 (
    .in_2(and_20_out), .in_3(and_28_out), .out_4(full_adder_3_out_4), .in_1(full_adder_2_out_5),
    .out_5(full_adder_3_out_5));
  full_adder full_adder_4 (
    .in_2(and_21_out), .in_3(and_29_out), .out_4(full_adder_4_out_4), .in_1(full_adder_3_out_5),
    .out_5(full_adder_4_out_5));
  full_adder full_adder_5 (
    .in_2(and_22_out), .in_3(and_30_out), .out_4(full_adder_5_out_4), .in_1(full_adder_4_out_5),
    .out_5(full_adder_5_out_5));
  full_adder full_adder_6 (
    .in_2(and_23_out), .in_3(and_31_out), .out_4(full_adder_6_out_4), .in_1(full_adder_5_out_5),
    .out_5(full_adder_6_out_5));
  full_adder full_adder_7 (
    .in_2(and_24_out), .in_3(and_32_out), .out_4(full_adder_7_out_4), .in_1(full_adder_6_out_5),
    .out_5(full_adder_7_out_5));
  multhelper multhelper_5 (.in_1({{8{1'b0}}, and_9_out}), .out_3(multhelper_5_out_3), .in_2(and_5_out));
  _16bitshift u_16bitshift_7 (.in_1(multhelper_5_out_3), .out_2(n16bitshift_7_out_2));
  _16bitshift u_16bitshift_8 (.in_1(n16bitshift_7_out_2), .out_2(n16bitshift_8_out_2));
  _16bitshift u_16bitshift_9 (.in_1(n16bitshift_8_out_2), .out_2(n16bitshift_9_out_2));
  _16bitshift u_16bitshift_10 (.in_1(n16bitshift_9_out_2), .out_2(n16bitshift_10_out_2));
  Adder #(.width(16)) adder_5 (.a(n16bitshift_10_out_2), .b(adder_4_out), .out(adder_5_out));  // open: cin, cout
  xor xor_1 (xor_1_out, full_adder_6_out_5, full_adder_7_out_5);
  multhelper multhelper_6 (.in_1({{8{1'b0}}, and_9_out}), .out_3(multhelper_6_out_3), .in_2(and_6_out));
  _16bitshift u_16bitshift_11 (.in_1(multhelper_6_out_3), .out_2(n16bitshift_11_out_2));
  _16bitshift u_16bitshift_12 (.in_1(n16bitshift_11_out_2), .out_2(n16bitshift_12_out_2));
  _16bitshift u_16bitshift_13 (.in_1(n16bitshift_12_out_2), .out_2(n16bitshift_13_out_2));
  _16bitshift u_16bitshift_14 (.in_1(n16bitshift_13_out_2), .out_2(n16bitshift_14_out_2));
  _16bitshift u_16bitshift_15 (.in_1(n16bitshift_14_out_2), .out_2(n16bitshift_15_out_2));
  Adder #(.width(16)) adder_6 (.a(n16bitshift_15_out_2), .b(adder_5_out), .out(adder_6_out));  // open: cin, cout
  multhelper multhelper_7 (.in_1({{8{1'b0}}, and_9_out}), .out_3(multhelper_7_out_3), .in_2(and_7_out));
  _16bitshift u_16bitshift_16 (.in_1(multhelper_7_out_3), .out_2(n16bitshift_16_out_2));
  _16bitshift u_16bitshift_17 (.in_1(n16bitshift_16_out_2), .out_2(n16bitshift_17_out_2));
  _16bitshift u_16bitshift_18 (.in_1(n16bitshift_17_out_2), .out_2(n16bitshift_18_out_2));
  _16bitshift u_16bitshift_19 (.in_1(n16bitshift_18_out_2), .out_2(n16bitshift_19_out_2));
  _16bitshift u_16bitshift_20 (.in_1(n16bitshift_19_out_2), .out_2(n16bitshift_20_out_2));
  _16bitshift u_16bitshift_21 (.in_1(n16bitshift_20_out_2), .out_2(n16bitshift_21_out_2));
  Adder #(.width(16)) adder_7 (.a(n16bitshift_21_out_2), .b(adder_6_out), .out(adder_7_out));  // open: cin, cout
  multhelper multhelper_8 (.in_1({{8{1'b0}}, and_9_out}), .out_3(multhelper_8_out_3), .in_2(and_8_out));
  _16bitshift u_16bitshift_22 (.in_1(multhelper_8_out_3), .out_2(n16bitshift_22_out_2));
  _16bitshift u_16bitshift_23 (.in_1(n16bitshift_22_out_2), .out_2(n16bitshift_23_out_2));
  _16bitshift u_16bitshift_24 (.in_1(n16bitshift_23_out_2), .out_2(n16bitshift_24_out_2));
  _16bitshift u_16bitshift_25 (.in_1(n16bitshift_24_out_2), .out_2(n16bitshift_25_out_2));
  _16bitshift u_16bitshift_26 (.in_1(n16bitshift_25_out_2), .out_2(n16bitshift_26_out_2));
  _16bitshift u_16bitshift_27 (.in_1(n16bitshift_26_out_2), .out_2(n16bitshift_27_out_2));
  _16bitshift u_16bitshift_28 (.in_1(n16bitshift_27_out_2), .out_2(n16bitshift_28_out_2));
  Adder #(.width(16)) adder_8 (.a(n16bitshift_28_out_2), .b(adder_7_out), .out(adder_8_out));  // open: cin, cout
  not not_1 (not_1_out, Overflow);
  and and_33 (Negative, not_1_out, out_9[7]);
  or or_2 (Overflow, or_3_out, xor_1_out);
  or or_3 (or_3_out, adder_8_out[8], adder_8_out[9], adder_8_out[10], adder_8_out[11], adder_8_out[12], adder_8_out[13], adder_8_out[14], adder_8_out[15]);
  or or_4 (out_9[0], half_adder_1_out_3, adder_8_out[0]);
  or or_5 (out_9[1], full_adder_1_out_4, adder_8_out[1]);
  or or_6 (out_9[2], full_adder_2_out_4, adder_8_out[2]);
  or or_7 (out_9[3], full_adder_3_out_4, adder_8_out[3]);
  or or_8 (out_9[4], full_adder_4_out_4, adder_8_out[4]);
  or or_9 (out_9[5], full_adder_5_out_4, adder_8_out[5]);
  or or_10 (out_9[6], full_adder_6_out_4, adder_8_out[6]);
  or or_11 (out_9[7], full_adder_7_out_4, adder_8_out[7]);
  not not_2 (not_2_out, out_9[2]);
  not not_3 (not_3_out, out_9[0]);
  not not_4 (not_4_out, out_9[1]);
  not not_5 (not_5_out, out_9[7]);
  not not_6 (not_6_out, out_9[3]);
  not not_7 (not_7_out, out_9[5]);
  not not_8 (not_8_out, out_9[4]);
  not not_9 (not_9_out, out_9[6]);
  and and_34 (Zero, not_3_out, not_4_out, not_2_out, not_6_out, not_8_out, not_7_out, not_9_out, not_5_out);

  // Notes on the sheet:
  //   R
  //   L
  //   SUB Section OPCODE required
  //   MULT SECTION OPCODE
  //   1 = SUB ON 0 = SUB OFF
  //   1= MULT ON 0= MULT OFF
  //   ADD Section OPCODE required
  //   1 = ADD ON 0 = ADD OFF
  //   Multiplication has no signed overflow check. Beware when using it with signed integers.
  //   If there is an overflow, we can't tell the sign.
endmodule

module full_adder (
  input  in_1,
  input  in_2,
  input  in_3,
  output out_4,
  output out_5
);

  wire and_1_out, and_2_out, xor_1_out;

  xor xor_1 (xor_1_out, in_2, in_3);
  and and_1 (and_1_out, in_1, xor_1_out);
  or or_1 (out_5, and_1_out, and_2_out);
  and and_2 (and_2_out, in_2, in_3);
  xor xor_2 (out_4, in_1, xor_1_out);
endmodule

module half_adder (
  input  in_1,
  input  in_2,
  output out_3,
  output out_4
);

  xor xor_1 (out_3, in_1, in_2);
  and and_1 (out_4, in_1, in_2);
endmodule

module ALU2C (
  input  in_1,
  input  [7:0] in_2,
  output [7:0] out_3
);

  wire and_1_out, and_2_out, and_3_out, and_4_out, and_5_out, and_6_out, and_7_out, and_8_out, and_9_out,
       and_10_out, and_11_out, and_12_out, and_13_out, and_14_out, and_15_out, and_16_out,
       full_adder_1_out_5, full_adder_2_out_5, full_adder_3_out_5, full_adder_4_out_5, full_adder_5_out_5,
       full_adder_6_out_5, half_adder_1_out_4, not_1_out, not_2_out, not_3_out, not_4_out, not_5_out,
       not_6_out, not_7_out, not_8_out, not_9_out, not_10_out, not_11_out, not_12_out, not_13_out,
       not_14_out, not_15_out, not_16_out, or_1_out, or_2_out, or_3_out, or_4_out, or_5_out, or_6_out,
       or_7_out, or_8_out;

  not not_1 (not_1_out, in_1);
  not not_2 (not_2_out, in_2[0]);
  not not_3 (not_3_out, in_1);
  not not_4 (not_4_out, in_2[1]);
  not not_5 (not_5_out, in_1);
  not not_6 (not_6_out, in_2[2]);
  not not_7 (not_7_out, in_1);
  not not_8 (not_8_out, in_2[3]);
  not not_9 (not_9_out, in_1);
  not not_10 (not_10_out, in_2[4]);
  not not_11 (not_11_out, in_1);
  not not_12 (not_12_out, in_2[5]);
  not not_13 (not_13_out, in_1);
  not not_14 (not_14_out, in_2[6]);
  not not_15 (not_15_out, in_1);
  not not_16 (not_16_out, in_2[7]);
  and and_1 (and_1_out, not_1_out, in_2[0]);
  or or_1 (or_1_out, and_1_out, and_2_out);
  and and_2 (and_2_out, in_1, not_2_out);
  and and_3 (and_3_out, not_3_out, in_2[1]);
  or or_2 (or_2_out, and_3_out, and_4_out);
  and and_4 (and_4_out, in_1, not_4_out);
  and and_5 (and_5_out, not_5_out, in_2[2]);
  or or_3 (or_3_out, and_5_out, and_6_out);
  and and_6 (and_6_out, in_1, not_6_out);
  and and_7 (and_7_out, not_7_out, in_2[3]);
  or or_4 (or_4_out, and_7_out, and_8_out);
  and and_8 (and_8_out, in_1, not_8_out);
  and and_9 (and_9_out, not_9_out, in_2[4]);
  or or_5 (or_5_out, and_9_out, and_10_out);
  and and_10 (and_10_out, in_1, not_10_out);
  and and_11 (and_11_out, not_11_out, in_2[5]);
  or or_6 (or_6_out, and_11_out, and_12_out);
  and and_12 (and_12_out, in_1, not_12_out);
  and and_13 (and_13_out, not_13_out, in_2[6]);
  or or_7 (or_7_out, and_13_out, and_14_out);
  and and_14 (and_14_out, in_1, not_14_out);
  and and_15 (and_15_out, not_15_out, in_2[7]);
  or or_8 (or_8_out, and_15_out, and_16_out);
  and and_16 (and_16_out, in_1, not_16_out);
  half_adder half_adder_1 (.in_1(or_1_out), .in_2(in_1), .out_3(out_3[0]), .out_4(half_adder_1_out_4));
  full_adder full_adder_1 (
    .in_2(or_2_out), .in_3(1'b0), .out_4(out_3[1]), .in_1(half_adder_1_out_4), .out_5(full_adder_1_out_5));
  full_adder full_adder_2 (
    .in_2(or_3_out), .in_3(1'b0), .out_4(out_3[2]), .in_1(full_adder_1_out_5), .out_5(full_adder_2_out_5));
  full_adder full_adder_3 (
    .in_2(or_4_out), .in_3(1'b0), .out_4(out_3[3]), .in_1(full_adder_2_out_5), .out_5(full_adder_3_out_5));
  full_adder full_adder_4 (
    .in_2(or_5_out), .in_3(1'b0), .out_4(out_3[4]), .in_1(full_adder_3_out_5), .out_5(full_adder_4_out_5));
  full_adder full_adder_5 (
    .in_2(or_6_out), .in_3(1'b0), .out_4(out_3[5]), .in_1(full_adder_4_out_5), .out_5(full_adder_5_out_5));
  full_adder full_adder_6 (
    .in_2(or_7_out), .in_3(1'b0), .out_4(out_3[6]), .in_1(full_adder_5_out_5), .out_5(full_adder_6_out_5));
  full_adder full_adder_7 (.in_2(or_8_out), .in_3(1'b0), .out_4(out_3[7]), .in_1(full_adder_6_out_5));  // open: out_5
endmodule

module _16bitshift (
  input  [15:0] in_1,
  output [15:0] out_2
);


  assign out_2 = {in_1[14:0], 1'b0};
endmodule

module multhelper (
  input  [15:0] in_1,
  input  in_2,
  output [15:0] out_3
);

  and and_1 (out_3[0], in_1[0], in_2);
  and and_2 (out_3[1], in_1[1], in_2);
  and and_3 (out_3[2], in_1[2], in_2);
  and and_4 (out_3[3], in_1[3], in_2);
  and and_5 (out_3[4], in_1[4], in_2);
  and and_6 (out_3[5], in_1[5], in_2);
  and and_7 (out_3[6], in_1[6], in_2);
  and and_8 (out_3[7], in_1[7], in_2);
  and and_9 (out_3[8], in_1[8], in_2);
  and and_10 (out_3[9], in_1[9], in_2);
  and and_11 (out_3[10], in_1[10], in_2);
  and and_12 (out_3[11], in_1[11], in_2);
  and and_13 (out_3[12], in_1[12], in_2);
  and and_14 (out_3[13], in_1[13], in_2);
  and and_15 (out_3[14], in_1[14], in_2);
  and and_16 (out_3[15], in_1[15], in_2);
endmodule

module StatusRegister (
  input  CLK,
  input  R_W,
  input  ENABLE,
  input  [2:0] INPUT,
  output [2:0] out_5
);

  wire and_1_out, and_2_out, and_3_out, and_4_out, and_5_out, not_1_out, not_2_out, not_3_out, not_4_out,
       s_r_ff_1_q, s_r_ff_2_q, s_r_ff_3_q;

  and and_1 (and_1_out, CLK, ENABLE);
  and and_2 (and_2_out, CLK, R_W, ENABLE);
  and and_3 (and_3_out, INPUT[0], CLK, R_W);
  not not_1 (not_1_out, and_3_out);
  and and_4 (and_4_out, INPUT[1], CLK, R_W);
  not not_2 (not_2_out, and_4_out);
  and and_5 (and_5_out, INPUT[2], CLK, R_W);
  not not_3 (not_3_out, and_5_out);
  not not_4 (not_4_out, R_W);
  S_R_Flip_Flop #(.trigger("high")) s_r_ff_1 (
    .S(and_3_out), .clk(and_2_out), .R(not_1_out), .Q(s_r_ff_1_q));  // open: Qn, preset, reset, en
  S_R_Flip_Flop #(.trigger("high")) s_r_ff_2 (
    .S(and_4_out), .clk(and_2_out), .R(not_2_out), .Q(s_r_ff_2_q));  // open: Qn, preset, reset, en
  S_R_Flip_Flop #(.trigger("high")) s_r_ff_3 (
    .S(and_5_out), .clk(and_2_out), .R(not_3_out), .Q(s_r_ff_3_q));  // open: Qn, preset, reset, en
  and and_6 (out_5[0], s_r_ff_1_q, and_1_out, not_4_out);
  and and_7 (out_5[1], s_r_ff_2_q, and_1_out, not_4_out);
  and and_8 (out_5[2], s_r_ff_3_q, and_1_out, not_4_out);
endmodule

module _3_Combinator (
  input  in_1,
  input  [7:0] in_2,
  input  in_3,
  input  [7:0] in_4,
  input  in_5,
  input  [7:0] in_6,
  output [7:0] out_7
);

  wire and_1_out, and_2_out, and_3_out, and_4_out, and_5_out, and_6_out, and_7_out, and_8_out, and_9_out,
       and_10_out, and_11_out, and_12_out, and_13_out, and_14_out, and_15_out, and_16_out, and_17_out,
       and_18_out, and_19_out, and_20_out, and_21_out, and_22_out, and_23_out, and_24_out;

  and and_1 (and_1_out, in_2[0], in_1);
  and and_2 (and_2_out, in_2[1], in_1);
  and and_3 (and_3_out, in_2[2], in_1);
  and and_4 (and_4_out, in_2[3], in_1);
  and and_5 (and_5_out, in_2[4], in_1);
  and and_6 (and_6_out, in_2[5], in_1);
  and and_7 (and_7_out, in_2[6], in_1);
  and and_8 (and_8_out, in_2[7], in_1);
  and and_9 (and_9_out, in_4[0], in_3);
  and and_10 (and_10_out, in_4[1], in_3);
  and and_11 (and_11_out, in_4[2], in_3);
  and and_12 (and_12_out, in_4[3], in_3);
  and and_13 (and_13_out, in_4[4], in_3);
  and and_14 (and_14_out, in_4[5], in_3);
  and and_15 (and_15_out, in_4[6], in_3);
  and and_16 (and_16_out, in_4[7], in_3);
  and and_17 (and_17_out, in_6[0], in_5);
  and and_18 (and_18_out, in_6[1], in_5);
  and and_19 (and_19_out, in_6[2], in_5);
  and and_20 (and_20_out, in_6[3], in_5);
  and and_21 (and_21_out, in_6[4], in_5);
  and and_22 (and_22_out, in_6[5], in_5);
  and and_23 (and_23_out, in_6[6], in_5);
  and and_24 (and_24_out, in_6[7], in_5);
  or or_1 (out_7[0], and_1_out, and_9_out, and_17_out);
  or or_2 (out_7[1], and_2_out, and_10_out, and_18_out);
  or or_3 (out_7[2], and_3_out, and_11_out, and_19_out);
  or or_4 (out_7[3], and_4_out, and_12_out, and_20_out);
  or or_5 (out_7[4], and_5_out, and_13_out, and_21_out);
  or or_6 (out_7[5], and_6_out, and_14_out, and_22_out);
  or or_7 (out_7[6], and_7_out, and_15_out, and_23_out);
  or or_8 (out_7[7], and_8_out, and_16_out, and_24_out);
endmodule

module _4_combinator (
  input  in_1,
  input  [7:0] in_2,
  input  in_3,
  input  [7:0] in_4,
  input  in_5,
  input  [7:0] in_6,
  input  in_7,
  input  [7:0] in_8,
  output [7:0] out_9
);

  wire and_1_out, and_2_out, and_3_out, and_4_out, and_5_out, and_6_out, and_7_out, and_8_out, and_9_out,
       and_10_out, and_11_out, and_12_out, and_13_out, and_14_out, and_15_out, and_16_out, and_17_out,
       and_18_out, and_19_out, and_20_out, and_21_out, and_22_out, and_23_out, and_24_out, and_25_out,
       and_26_out, and_27_out, and_28_out, and_29_out, and_30_out, and_31_out, and_32_out;

  and and_1 (and_1_out, in_2[0], in_1);
  and and_2 (and_2_out, in_2[1], in_1);
  and and_3 (and_3_out, in_2[2], in_1);
  and and_4 (and_4_out, in_2[3], in_1);
  and and_5 (and_5_out, in_2[4], in_1);
  and and_6 (and_6_out, in_2[5], in_1);
  and and_7 (and_7_out, in_2[6], in_1);
  and and_8 (and_8_out, in_2[7], in_1);
  and and_9 (and_9_out, in_4[0], in_3);
  and and_10 (and_10_out, in_4[1], in_3);
  and and_11 (and_11_out, in_4[2], in_3);
  and and_12 (and_12_out, in_4[3], in_3);
  and and_13 (and_13_out, in_4[4], in_3);
  and and_14 (and_14_out, in_4[5], in_3);
  and and_15 (and_15_out, in_4[6], in_3);
  and and_16 (and_16_out, in_4[7], in_3);
  and and_17 (and_17_out, in_6[0], in_5);
  and and_18 (and_18_out, in_6[1], in_5);
  and and_19 (and_19_out, in_6[2], in_5);
  and and_20 (and_20_out, in_6[3], in_5);
  and and_21 (and_21_out, in_6[4], in_5);
  and and_22 (and_22_out, in_6[5], in_5);
  and and_23 (and_23_out, in_6[6], in_5);
  and and_24 (and_24_out, in_6[7], in_5);
  and and_25 (and_25_out, in_8[0], in_7);
  and and_26 (and_26_out, in_8[1], in_7);
  and and_27 (and_27_out, in_8[2], in_7);
  and and_28 (and_28_out, in_8[3], in_7);
  and and_29 (and_29_out, in_8[4], in_7);
  and and_30 (and_30_out, in_8[5], in_7);
  and and_31 (and_31_out, in_8[6], in_7);
  and and_32 (and_32_out, in_8[7], in_7);
  or or_1 (out_9[0], and_1_out, and_9_out, and_17_out, and_25_out);
  or or_2 (out_9[1], and_2_out, and_10_out, and_18_out, and_26_out);
  or or_3 (out_9[2], and_3_out, and_11_out, and_19_out, and_27_out);
  or or_4 (out_9[3], and_4_out, and_12_out, and_20_out, and_28_out);
  or or_5 (out_9[4], and_5_out, and_13_out, and_21_out, and_29_out);
  or or_6 (out_9[5], and_6_out, and_14_out, and_22_out, and_30_out);
  or or_7 (out_9[6], and_7_out, and_15_out, and_23_out, and_31_out);
  or or_8 (out_9[7], and_8_out, and_16_out, and_24_out, and_32_out);
endmodule
