// Logisim project CPU.circ as structural Verilog: 33 circuits, main circuit main
module main (
  input  in_1,
  input  in_2,
  input  in_3,
  input  in_4,
  input  in_5,
  input  in_6,
  input  in_7,
  input  in_8,
  input  in_9,
  input  From_PC,
  input  _1___INSTR_MAR,
  input  in_12,
  input  in_13,
  input  RAM_EN,
  input  [2:0] in_15,
  input  Send_to_Sys_BUS,
  input  SYS_FROM_DR,
  input  Send_to_IR,
  input  in_19,
  input  SYS_FROM_MAR,
  input  in_21,
  input  From_MBR,
  input  in_23,
  input  SYS_FROM_MBR,
  input  in_25,
  input  [9:0] PINS_0_to_9,
  input  in_27,
  input  ENABLE,
  input  in_29,
  input  in_30,
  input  in_31,
  input  in_32,
  input  in_33,
  input  in_34,
  input  in_35,
  input  in_36,
  input  in_37,
  input  in_38,
  input  in_39,
  input  in_40,
  input  in_41,
  input  in_42,
  input  in_43,
  output [7:0] SYSTEM_BUS,
  output out_45,
  output [7:0] CPU_BUS
);

  wire and_1_out, clock_1_out, display_1_a, display_1_b, display_1_c, display_1_d, display_1_e, display_1_f,
       display_1_g, display_2_a, display_2_b, display_2_c, display_2_d, display_2_e, display_2_f,
       display_2_g, display_3_a, display_3_b, display_3_c, display_3_d, display_3_e, display_3_f,
       display_3_g, memory_control_unit_1_ar_clk, memory_control_unit_1_ar_enable,
       memory_control_unit_1_ar_r_w, memory_control_unit_1_dr_clk, memory_control_unit_1_dr_direction,
       memory_control_unit_1_dr_enable, memory_control_unit_1_dr_r_w, memory_control_unit_1_ram_clk,
       memory_control_unit_1_ram_r_w, not_1_out, not_2_out;
  wire [1:0] or_2_out;
  wire [2:0] alu_1_overflow, statusregister_1_out_5;
  wire [3:0] compressor_1_out_2, makingbdc_1_out_3, makingbdc_1_out_4, makingbdc_1_out_5, register_7_out_5;
  wire [7:0] alu_1_out_9, demultiplexer_1_out1, demultiplexer_1_out2, demultiplexer_1_out3, dr_1_output1,
       dr_1_output2, incrementer_1_out_2, keypad_buttons_and_outputs_1_out_12,
       memory_control_unit_1_ar_input, memory_control_unit_1_dr_input, multiplexer_1_out,
       n2_combinator_1_out_5, n3_combinator_1_out_7, n5_combinator_2_out_11, pcregister_1_out_7,
       ram_project_1_out_15, register_1_out_5, register_2_out_5, register_3_out_5, register_4_out_5,
       register_5_out_5, register_6_out_5, register_8_out_5, register_9_out_5, register_10_out_5,
       registers_1_out_5, undriven;
  wire [7:4] register_7_out_5_2;

  compressor compressor_1 (.in_1(registers_1_out_5), .out_2(compressor_1_out_2));
  makingBDC makingbdc_1 (
    .in_2(n3_combinator_1_out_7), .ENABLE(ENABLE), .out_3(makingbdc_1_out_3), .out_4(makingbdc_1_out_4),
    .out_5(makingbdc_1_out_5));
  RAM_project ram_project_1 (
    .DATA(dr_1_output1[0]), .in_8(dr_1_output1[1]), .in_9(dr_1_output1[2]), .in_10(dr_1_output1[3]),
    .in_11(dr_1_output1[4]), .in_12(dr_1_output1[5]), .in_13(dr_1_output1[6]), .in_14(dr_1_output1[7]),
    .ADDR(compressor_1_out_2[3]), .in_2(compressor_1_out_2[2]), .in_3(compressor_1_out_2[1]),
    .in_4(compressor_1_out_2[0]), .RW(memory_control_unit_1_ram_r_w), .CLK(memory_control_unit_1_ram_clk),
    .out_15(ram_project_1_out_15));
  registers registers_1 (
    .CLK(memory_control_unit_1_ar_clk), .R_W(memory_control_unit_1_ar_r_w),
    .ENABLE(memory_control_unit_1_ar_enable), .INPUT(memory_control_unit_1_ar_input),
    .out_5(registers_1_out_5));
  DR dr_1 (
    .CLK(memory_control_unit_1_dr_clk), .R_W(memory_control_unit_1_dr_r_w),
    .ENABLE(memory_control_unit_1_dr_enable), .INPUT_1(memory_control_unit_1_dr_input),
    .in_5(memory_control_unit_1_dr_direction), .INPUT_2(ram_project_1_out_15), .OUTPUT1(dr_1_output1),
    .OUTPUT2(dr_1_output2));
  keypad_buttons_and_outputs keypad_buttons_and_outputs_1 (
    ._0(PINS_0_to_9[0]), ._1(PINS_0_to_9[1]), ._2(PINS_0_to_9[2]), ._3(PINS_0_to_9[3]), ._4(PINS_0_to_9[4]),
    ._5(PINS_0_to_9[5]), ._6(PINS_0_to_9[6]), ._7(PINS_0_to_9[7]), ._8(PINS_0_to_9[8]), ._9(PINS_0_to_9[9]),
    .ENTER(in_27), .out_12(keypad_buttons_and_outputs_1_out_12));
  display display_1 (
    .d(display_1_d), .e(display_1_e), .g(display_1_g), .b(display_1_b), .a(display_1_a), .c(display_1_c),
    .f(display_1_f), .in_1(makingbdc_1_out_3));
  display display_2 (
    .d(display_2_d), .e(display_2_e), .g(display_2_g), .b(display_2_b), .a(display_2_a), .c(display_2_c),
    .f(display_2_f), .in_1(makingbdc_1_out_4));
  display display_3 (
    .d(display_3_d), .e(display_3_e), .g(display_3_g), .b(display_3_b), .a(display_3_a), .c(display_3_c),
    .f(display_3_f), .in_1(makingbdc_1_out_5));
  register register_1 (
    .CLK(clock_1_out), .R_W(in_25), .ENABLE(SYS_FROM_MBR), .INPUT(keypad_buttons_and_outputs_1_out_12),
    .out_5(register_1_out_5));
  _7_Segment_Display u_7_segment_display_1 (
    .g(display_3_d), .f(display_3_b), .a(display_3_a), .b(display_3_c), .e(display_3_e), .d(display_3_g),
    .c(display_3_f));  // open: dp
  _7_Segment_Display u_7_segment_display_2 (
    .g(display_2_d), .f(display_2_b), .a(display_2_a), .b(display_2_c), .e(display_2_e), .d(display_2_g),
    .c(display_2_f));  // open: dp
  _7_Segment_Display u_7_segment_display_3 (
    .g(display_1_d), .f(display_1_b), .a(display_1_a), .b(display_1_c), .e(display_1_e), .d(display_1_g),
    .c(display_1_f));  // open: dp
  MEMORY_CONTROL_UNIT memory_control_unit_1 (
    .bit2(in_15[0]), .bit1(in_15[1]), .bit0(in_15[2]), .AR_INPUT(memory_control_unit_1_ar_input),
    .AR_CLK(memory_control_unit_1_ar_clk), .AR_R_W(memory_control_unit_1_ar_r_w),
    .AR_ENABLE(memory_control_unit_1_ar_enable), .RAM_CLK(memory_control_unit_1_ram_clk),
    .RAM_R_W(memory_control_unit_1_ram_r_w), .DR_INPUT(memory_control_unit_1_dr_input),
    .DR_CLK(memory_control_unit_1_dr_clk), .DR_R_W(memory_control_unit_1_dr_r_w),
    .DR_ENABLE(memory_control_unit_1_dr_enable), .DR_DIRECTION(memory_control_unit_1_dr_direction),
    .INPUT(n3_combinator_1_out_7), .ENABLE(RAM_EN), .DONE_FLAG(out_45), .CLOCK(clock_1_out));
  _4_combinator u_4_combinator_1 (
    .in_2(dr_1_output2), .in_4(register_1_out_5), .in_6(register_2_out_5), .in_8(demultiplexer_1_out2),
    .out_9(SYSTEM_BUS), .in_1(SYS_FROM_DR), .in_3(in_19), .in_5(SYS_FROM_MAR), .in_7(in_23));
  _3_Combinator u_3_combinator_1 (
    .in_2(SYSTEM_BUS), .in_4(SYSTEM_BUS), .in_6(SYSTEM_BUS), .out_7(n3_combinator_1_out_7), .in_1(ENABLE),
    .in_3(RAM_EN), .in_5(and_1_out));
  Clock clock_1 (.out(clock_1_out));
  Button CLOCK_2 ();  // open: out
  CU cu_1 ();  // open: D0_EN, D0_RW, D1_EN, D1_RW, L_EN, L_RW, R_EN, R_RW, A_EN, A_RW, STATUS_EN, STATUS_RW, MBR_EN, MBR_RW, MAR_EN, MAR_RW, in_1, STATUS_ZERO_FLAG, OP_CODE
  and and_1 (and_1_out, in_6, in_5, in_7);
  _2_Combinator u_2_combinator_1 (
    .in_2(n3_combinator_1_out_7), .in_4(undriven), .out_5(n2_combinator_1_out_5), .in_1(not_1_out),
    .in_3(in_21));
  not not_1 (not_1_out, in_21);
  register register_2 (
    .CLK(clock_1_out), .R_W(in_8), .ENABLE(in_9), .INPUT(multiplexer_1_out), .out_5(register_2_out_5));
  register register_3 (
    .CLK(clock_1_out), .R_W(in_7), .ENABLE(in_6), .INPUT(n2_combinator_1_out_5), .out_5(register_3_out_5));
  register register_4 (
    .CLK(clock_1_out), .R_W(in_35), .ENABLE(in_36), .INPUT(n5_combinator_2_out_11), .out_5(register_4_out_5));
  register register_5 (
    .CLK(clock_1_out), .R_W(in_40), .ENABLE(in_41), .INPUT(n5_combinator_2_out_11), .out_5(register_5_out_5));
  Multiplexer #(.width(8), .disabled(0), .enable("false")) multiplexer_1 (
    .in0(pcregister_1_out_7), .in1({4'b0000, register_7_out_5}), .out(multiplexer_1_out), .sel(_1___INSTR_MAR));
  Demultiplexer #(.select(2), .width(8), .disabled(0), .enable("false")) demultiplexer_1 (
    .out1(demultiplexer_1_out1), .out2(demultiplexer_1_out2), .out3(demultiplexer_1_out3),
    .in(register_3_out_5), .sel(or_2_out));  // open: out0
  or or_1 (or_2_out[1], Send_to_Sys_BUS, Send_to_IR);
  or or_2 (or_2_out[0], Send_to_IR, From_MBR);
  Incrementer incrementer_1 (.in_1(pcregister_1_out_7), .out_2(incrementer_1_out_2));
  _5_combinator u_5_combinator_1 (
    .in_2({{5{1'b0}}, statusregister_1_out_5}), .in_4(register_10_out_5), .in_6(register_4_out_5),
    .in_8(register_5_out_5), .in_10(undriven), .out_11(CPU_BUS), .in_1(in_34), .in_3(in_42), .in_5(in_36),
    .in_7(in_41), .in_9(in_21));
  StatusRegister statusregister_1 (
    .CLK(clock_1_out), .R_W(in_33), .ENABLE(in_34), .INPUT(alu_1_overflow), .out_5(statusregister_1_out_5));
  register register_6 (
    .CLK(clock_1_out), .R_W(in_4), .ENABLE(in_3), .INPUT(incrementer_1_out_2), .out_5(register_6_out_5));
  register register_7 (
    .CLK(clock_1_out), .R_W(in_12), .ENABLE(in_13), .INPUT(demultiplexer_1_out3),
    .out_5({register_7_out_5_2, register_7_out_5}));
  register register_8 (
    .CLK(clock_1_out), .R_W(in_30), .ENABLE(in_29), .INPUT(n5_combinator_2_out_11), .out_5(register_8_out_5));
  register register_9 (
    .CLK(clock_1_out), .R_W(in_32), .ENABLE(in_31), .INPUT(n5_combinator_2_out_11), .out_5(register_9_out_5));
  ALU alu_1 (
    .in_3(register_9_out_5), .in_4(register_8_out_5), .in_5(in_39), .in_2(in_37), .in_1(in_38),
    .Overflow(alu_1_overflow[0]), .Zero(alu_1_overflow[1]), .Negative(alu_1_overflow[2]), .out_9(alu_1_out_9));
  register register_10 (.CLK(clock_1_out), .R_W(in_43), .ENABLE(in_42), .INPUT(alu_1_out_9), .out_5(register_10_out_5));
  PCregister pcregister_1 (
    .CLK(clock_1_out), .R_W(in_2), .ENABLE(in_1), .in_4(register_6_out_5), .out_7(pcregister_1_out_7),
    .in_5(register_7_out_5[2:0]), .in_6(not_2_out));
  not not_2 (not_2_out, From_PC);
  _5_combinator u_5_combinator_2 (
    .in_2(CPU_BUS), .in_4(CPU_BUS), .in_6(CPU_BUS), .in_8(CPU_BUS), .in_10(demultiplexer_1_out1),
    .out_11(n5_combinator_2_out_11), .in_1(in_29), .in_3(in_31), .in_5(in_36), .in_7(in_41), .in_9(From_MBR));

  // Notes on the sheet:
  //   SYS FROM INPUT
  //   Device connected to CPU bus that receive data:
  //   RAM
  //   MBR
  //   DISPLAY
  //   Device connected to CPU bus that send data
  //   RAM DR
  //   input
  //   MAR
  //   MBR
  //   RAM commands
  //   From Sys BUS TO MBR
  //   AR
  //   To DR
  //   From DR
  //   Bit from status register when 0
  //   MAR
  //   MBR
  //   D0
  //   D1
  //   beq bnq flag
  //   TO SYS BUS (DR)
  //   Send to CPU BUS
  //   To MBR
  //   Temp Reg for PC, PCT
  //   0 - PC - MAR
  //   TO INSTR
  //   TO MBR
  //   INSTR
  //   INSTR REG
  //   L Register
  //   A out
  //   TO CU
  //   R Register
  //   Should be ON for t he 6 ticks of execute
  //   CU sends 3 bit addr when beq,bnq are used.
endmodule

module RAM_project (
  input  ADDR,
  input  in_2,
  input  in_3,
  input  in_4,
  input  CLK,
  input  RW,
  input  DATA,
  input  in_8,
  input  in_9,
  input  in_10,
  input  in_11,
  input  in_12,
  input  in_13,
  input  in_14,
  output [7:0] out_15
);

  wire and_1_out, and_2_out, and_3_out, and_4_out, and_5_out, and_6_out, and_7_out, and_8_out, and_9_out,
       and_10_out, and_11_out, and_12_out, and_13_out, and_14_out, and_15_out, and_16_out, and_17_out,
       and_26_out, n4to16_1_addr0, n4to16_1_addr1, n4to16_1_addr2, n4to16_1_addr3, n4to16_1_addr4,
       n4to16_1_addr5, n4to16_1_addr6, n4to16_1_addr7, n4to16_1_addr8, n4to16_1_addr9, n4to16_1_addr10,
       n4to16_1_addr11, n4to16_1_addr12, n4to16_1_addr13, n4to16_1_addr14, n4to16_1_addr15, not_1_out,
       not_2_out, not_3_out, not_4_out, not_5_out, not_6_out, not_7_out, not_8_out, not_9_out, not_10_out,
       not_11_out, not_12_out, not_13_out, not_14_out, not_15_out, not_16_out, not_17_out, not_18_out,
       not_19_out, not_20_out, not_21_out, not_22_out, not_23_out, or_1_out, or_2_out, or_3_out, or_4_out,
       or_5_out, or_6_out, or_7_out, or_8_out, s_r_ff_1_q, s_r_ff_2_q, s_r_ff_3_q, s_r_ff_4_q, s_r_ff_5_q,
       s_r_ff_6_q, s_r_ff_6_qn, s_r_ff_7_q, s_r_ff_7_qn, s_r_ff_8_q, s_r_ff_8_qn, s_r_ff_9_q, s_r_ff_9_qn,
       s_r_ff_10_q, s_r_ff_10_qn, s_r_ff_11_q, s_r_ff_11_qn, s_r_ff_12_q, s_r_ff_12_qn, s_r_ff_13_q,
       s_r_ff_13_qn;
  wire [7:0] and_25_out, byte0_outputbits, byte1_outputbits, byte2_outputbits, byte3_outputbits,
       byte4_outputbits, byte6_outputbits, byte7_outputbits, byte8_outputbits, byte9_outputbits,
       byte10_outputbits, byte11_outputbits, byte12_outputbits, byte13_outputbits, byte14_outputbits,
       byte15_2_outputbits, byte15_outputbits, combinator_1_out_17;

  not not_1 (not_1_out, RW);
  and and_1 (and_1_out, DATA, RW);
  and and_2 (and_2_out, in_8, RW);
  and and_3 (and_3_out, in_9, RW);
  and and_4 (and_4_out, in_10, RW);
  and and_5 (and_5_out, in_11, RW);
  and and_6 (and_6_out, in_12, RW);
  and and_7 (and_7_out, in_13, RW);
  and and_8 (and_8_out, in_14, RW);
  and and_9 (and_9_out, combinator_1_out_17[0], not_1_out);
  and and_10 (and_10_out, combinator_1_out_17[3], not_1_out);
  and and_11 (and_11_out, combinator_1_out_17[2], not_1_out);
  and and_12 (and_12_out, combinator_1_out_17[1], not_1_out);
  S_R_Flip_Flop s_r_ff_1 (.Q(s_r_ff_1_q), .preset(in_4), .reset(not_2_out));  // open: S, clk, R, Qn, en
  not not_2 (not_2_out, in_4);
  S_R_Flip_Flop s_r_ff_2 (.Q(s_r_ff_2_q), .preset(in_3), .reset(not_3_out));  // open: S, clk, R, Qn, en
  not not_3 (not_3_out, in_3);
  S_R_Flip_Flop s_r_ff_3 (.Q(s_r_ff_3_q), .preset(in_2), .reset(not_4_out));  // open: S, clk, R, Qn, en
  not not_4 (not_4_out, in_2);
  S_R_Flip_Flop s_r_ff_4 (.Q(s_r_ff_4_q), .preset(ADDR), .reset(not_5_out));  // open: S, clk, R, Qn, en
  not not_5 (not_5_out, ADDR);
  S_R_Flip_Flop s_r_ff_5 (.Q(s_r_ff_5_q), .preset(RW), .reset(not_6_out));  // open: S, clk, R, Qn, en
  not not_6 (not_6_out, RW);
  and and_13 (and_13_out, combinator_1_out_17[5], not_1_out);
  and and_14 (and_14_out, combinator_1_out_17[4], not_1_out);
  not not_7 (not_7_out, s_r_ff_5_q);
  and and_15 (and_15_out, combinator_1_out_17[6], not_1_out);
  and and_16 (and_16_out, combinator_1_out_17[7], not_1_out);
  or or_1 (or_1_out, and_1_out, and_9_out);
  or or_2 (or_2_out, and_2_out, and_12_out);
  or or_3 (or_3_out, and_3_out, and_11_out);
  or or_4 (or_4_out, and_4_out, and_10_out);
  or or_5 (or_5_out, and_5_out, and_14_out);
  or or_6 (or_6_out, and_6_out, and_13_out);
  or or_7 (or_7_out, and_7_out, and_15_out);
  or or_8 (or_8_out, and_8_out, and_16_out);
  and and_17 (and_17_out, CLK, s_r_ff_5_q);
  S_R_Flip_Flop #(.trigger("high")) s_r_ff_6 (
    .S(or_1_out), .clk(CLK), .R(not_8_out), .Q(s_r_ff_6_q), .Qn(s_r_ff_6_qn));  // open: preset, reset, en
  not not_8 (not_8_out, or_1_out);
  S_R_Flip_Flop #(.trigger("high")) s_r_ff_7 (
    .S(or_2_out), .clk(CLK), .R(not_9_out), .Q(s_r_ff_7_q), .Qn(s_r_ff_7_qn));  // open: preset, reset, en
  not not_9 (not_9_out, or_2_out);
  S_R_Flip_Flop #(.trigger("high")) s_r_ff_8 (
    .S(or_3_out), .clk(CLK), .R(not_10_out), .Q(s_r_ff_8_q), .Qn(s_r_ff_8_qn));  // open: preset, reset, en
  not not_10 (not_10_out, or_3_out);
  S_R_Flip_Flop #(.trigger("high")) s_r_ff_9 (
    .S(or_4_out), .clk(CLK), .R(not_11_out), .Q(s_r_ff_9_q), .Qn(s_r_ff_9_qn));  // open: preset, reset, en
  not not_11 (not_11_out, or_4_out);
  S_R_Flip_Flop #(.trigger("high")) s_r_ff_10 (
    .S(or_5_out), .clk(CLK), .R(not_12_out), .Q(s_r_ff_10_q), .Qn(s_r_ff_10_qn));  // open: preset, reset, en
  not not_12 (not_12_out, or_5_out);
  S_R_Flip_Flop #(.trigger("high")) s_r_ff_11 (
    .S(or_6_out), .clk(CLK), .R(not_13_out), .Q(s_r_ff_11_q), .Qn(s_r_ff_11_qn));  // open: preset, reset, en
  not not_13 (not_13_out, or_6_out);
  S_R_Flip_Flop #(.trigger("high")) s_r_ff_12 (
    .S(or_7_out), .clk(CLK), .R(not_14_out), .Q(s_r_ff_12_q), .Qn(s_r_ff_12_qn));  // open: preset, reset, en
  not not_14 (not_14_out, or_7_out);
  S_R_Flip_Flop #(.trigger("high")) s_r_ff_13 (
    .S(or_8_out), .clk(CLK), .R(not_15_out), .Q(s_r_ff_13_q), .Qn(s_r_ff_13_qn));  // open: preset, reset, en
  not not_15 (not_15_out, or_8_out);
  _4to16 u_4to16_1 (
    .value(CLK), .bit3(s_r_ff_4_q), .bit2(s_r_ff_3_q), .bit1(s_r_ff_2_q), .bit0(s_r_ff_1_q),
    .ADDR0(n4to16_1_addr0), .ADDR1(n4to16_1_addr1), .ADDR2(n4to16_1_addr2), .ADDR3(n4to16_1_addr3),
    .ADDR4(n4to16_1_addr4), .ADDR5(n4to16_1_addr5), .ADDR6(n4to16_1_addr6), .ADDR7(n4to16_1_addr7),
    .ADDR8(n4to16_1_addr8), .ADDR9(n4to16_1_addr9), .ADDR10(n4to16_1_addr10), .ADDR11(n4to16_1_addr11),
    .ADDR12(n4to16_1_addr12), .ADDR13(n4to16_1_addr13), .ADDR14(n4to16_1_addr14), .ADDR15(n4to16_1_addr15));
  and and_18 (and_25_out[6], s_r_ff_7_q, and_17_out);
  and and_19 (and_25_out[7], s_r_ff_6_q, and_17_out);
  and and_20 (and_25_out[3], s_r_ff_10_q, and_17_out);
  and and_21 (and_25_out[4], s_r_ff_9_q, and_17_out);
  and and_22 (and_25_out[5], s_r_ff_8_q, and_17_out);
  and and_23 (and_25_out[2], s_r_ff_11_q, and_17_out);
  and and_24 (and_25_out[1], s_r_ff_12_q, and_17_out);
  and and_25 (and_25_out[0], s_r_ff_13_q, and_17_out);
  and and_26 (and_26_out, CLK, not_7_out);
  not not_16 (not_16_out, s_r_ff_6_qn);
  not not_17 (not_17_out, s_r_ff_7_qn);
  not not_18 (not_18_out, s_r_ff_8_qn);
  not not_19 (not_19_out, s_r_ff_9_qn);
  not not_20 (not_20_out, s_r_ff_10_qn);
  not not_21 (not_21_out, s_r_ff_11_qn);
  not not_22 (not_22_out, s_r_ff_12_qn);
  not not_23 (not_23_out, s_r_ff_13_qn);
  and and_27 (out_15[0], and_26_out, not_16_out);
  and and_28 (out_15[1], and_26_out, not_17_out);
  and and_29 (out_15[2], and_26_out, not_18_out);
  and and_30 (out_15[3], and_26_out, not_19_out);
  and and_31 (out_15[4], and_26_out, not_20_out);
  and and_32 (out_15[5], and_26_out, not_21_out);
  and and_33 (out_15[6], and_26_out, not_22_out);
  and and_34 (out_15[7], and_26_out, not_23_out);
  \byte  byte0 (
    .InputBits(and_25_out), .Outputbits(byte0_outputbits), .CLOCK(CLK), .RW(and_17_out), .EN(n4to16_1_addr0));
  \byte  byte1 (
    .InputBits(and_25_out), .Outputbits(byte1_outputbits), .CLOCK(CLK), .RW(and_17_out), .EN(n4to16_1_addr1));
  \byte  byte2 (
    .InputBits(and_25_out), .Outputbits(byte2_outputbits), .CLOCK(CLK), .RW(and_17_out), .EN(n4to16_1_addr2));
  \byte  byte3 (
    .InputBits(and_25_out), .Outputbits(byte3_outputbits), .CLOCK(CLK), .RW(and_17_out), .EN(n4to16_1_addr3));
  \byte  byte4 (
    .InputBits(and_25_out), .Outputbits(byte4_outputbits), .CLOCK(CLK), .RW(and_17_out), .EN(n4to16_1_addr4));
  \byte  byte6 (
    .InputBits(and_25_out), .Outputbits(byte6_outputbits), .CLOCK(CLK), .RW(and_17_out), .EN(n4to16_1_addr5));
  \byte  byte7 (
    .InputBits(and_25_out), .Outputbits(byte7_outputbits), .CLOCK(CLK), .RW(and_17_out), .EN(n4to16_1_addr6));
  \byte  byte8 (
    .InputBits(and_25_out), .Outputbits(byte8_outputbits), .CLOCK(CLK), .RW(and_17_out), .EN(n4to16_1_addr7));
  \byte  byte9 (
    .InputBits(and_25_out), .Outputbits(byte9_outputbits), .CLOCK(CLK), .RW(and_17_out), .EN(n4to16_1_addr8));
  \byte  byte10 (
    .InputBits(and_25_out), .Outputbits(byte10_outputbits), .CLOCK(CLK), .RW(and_17_out), .EN(n4to16_1_addr9));
  \byte  byte11 (
    .InputBits(and_25_out), .Outputbits(byte11_outputbits), .CLOCK(CLK), .RW(and_17_out), .EN(n4to16_1_addr10));
  \byte  byte12 (
    .InputBits(and_25_out), .Outputbits(byte12_outputbits), .CLOCK(CLK), .RW(and_17_out), .EN(n4to16_1_addr11));
  \byte  byte13 (
    .InputBits(and_25_out), .Outputbits(byte13_outputbits), .CLOCK(CLK), .RW(and_17_out), .EN(n4to16_1_addr12));
  \byte  byte14 (
    .InputBits(and_25_out), .Outputbits(byte14_outputbits), .CLOCK(CLK), .RW(and_17_out), .EN(n4to16_1_addr13));
  \byte  byte15 (
    .InputBits(and_25_out), .Outputbits(byte15_outputbits), .CLOCK(CLK), .RW(and_17_out), .EN(n4to16_1_addr14));
  \byte  byte15_2 (
    .InputBits(and_25_out), .Outputbits(byte15_2_outputbits), .CLOCK(CLK), .RW(and_17_out),
    .EN(n4to16_1_addr15));
  COMBINATOR combinator_1 (
    .in_1(byte15_2_outputbits), .in_2(byte15_outputbits), .in_3(byte14_outputbits), .in_4(byte13_outputbits),
    .in_5(byte12_outputbits), .in_6(byte11_outputbits), .in_7(byte10_outputbits), .in_8(byte9_outputbits),
    .in_9(byte8_outputbits), .in_10(byte7_outputbits), .in_11(byte6_outputbits), .in_12(byte4_outputbits),
    .in_13(byte3_outputbits), .in_14(byte2_outputbits), .in_15(byte1_outputbits), .in_16(byte0_outputbits),
    .out_17(combinator_1_out_17));
endmodule

module _4to16 (
  input  value,
  input  bit3,
  input  bit2,
  input  bit1,
  input  bit0,
  output ADDR0,
  output ADDR1,
  output ADDR2,
  output ADDR3,
  output ADDR4,
  output ADDR5,
  output ADDR6,
  output ADDR7,
  output ADDR8,
  output ADDR9,
  output ADDR10,
  output ADDR11,
  output ADDR12,
  output ADDR13,
  output ADDR14,
  output ADDR15
);

  wire not_1_out, not_2_out, not_3_out, not_4_out, not_5_out, not_6_out, not_7_out, not_8_out, not_9_out,
       not_10_out, not_11_out, not_12_out, not_13_out, not_14_out, not_15_out, not_16_out, not_17_out,
       not_18_out, not_19_out, not_20_out, not_21_out, not_22_out, not_23_out, not_24_out, not_25_out,
       not_26_out, not_27_out, not_28_out, not_29_out, not_30_out, not_31_out, not_32_out;

  not not_1 (not_1_out, bit0);
  not not_2 (not_2_out, bit1);
  not not_3 (not_3_out, bit3);
  not not_4 (not_4_out, bit2);
  not not_5 (not_5_out, bit1);
  not not_6 (not_6_out, bit2);
  and u_addr1 (ADDR1, bit0, not_5_out, not_6_out, not_7_out, value);
  and u_addr0 (ADDR0, not_1_out, not_2_out, not_4_out, not_3_out, value);
  not not_7 (not_7_out, bit3);
  not not_8 (not_8_out, bit2);
  not not_9 (not_9_out, bit0);
  not not_10 (not_10_out, bit3);
  and u_addr2 (ADDR2, not_9_out, bit1, not_8_out, not_10_out, value);
  not not_11 (not_11_out, bit3);
  not not_12 (not_12_out, bit2);
  and u_addr3 (ADDR3, bit0, bit1, not_12_out, not_11_out, value);
  not not_13 (not_13_out, bit1);
  not not_14 (not_14_out, bit0);
  not not_15 (not_15_out, bit3);
  and u_addr4 (ADDR4, not_14_out, not_13_out, bit2, not_15_out, value);
  not not_16 (not_16_out, bit1);
  not not_17 (not_17_out, bit3);
  and u_addr5 (ADDR5, bit0, not_16_out, bit2, not_17_out, value);
  not not_18 (not_18_out, bit0);
  not not_19 (not_19_out, bit3);
  and u_addr6 (ADDR6, not_18_out, bit1, bit2, not_19_out, value);
  not not_20 (not_20_out, bit0);
  not not_21 (not_21_out, bit1);
  not not_22 (not_22_out, bit3);
  and u_addr7 (ADDR7, bit0, bit1, bit2, not_22_out, value);
  not not_23 (not_23_out, bit1);
  not not_24 (not_24_out, bit2);
  not not_25 (not_25_out, bit2);
  and u_addr9 (ADDR9, bit0, not_23_out, not_24_out, bit3, value);
  and u_addr8 (ADDR8, not_20_out, not_21_out, not_25_out, bit3, value);
  not not_26 (not_26_out, bit2);
  not not_27 (not_27_out, bit0);
  and add10 (ADDR10, not_27_out, bit1, not_26_out, bit3, value);
  not not_28 (not_28_out, bit2);
  and u_addr11 (ADDR11, bit0, bit1, not_28_out, bit3, value);
  not not_29 (not_29_out, bit0);
  not not_30 (not_30_out, bit1);
  and u_addr12 (ADDR12, not_29_out, not_30_out, bit2, bit3, value);
  not not_31 (not_31_out, bit1);
  and u_addr13 (ADDR13, bit0, not_31_out, bit2, bit3, value);
  not not_32 (not_32_out, bit0);
  and u_addr14 (ADDR14, not_32_out, bit1, bit2, bit3, value);
  and u_addr15 (ADDR15, bit0, bit1, bit2, bit3, value);

  // Notes on the sheet:
  //   2
endmodule

module COMBINATOR (
  input  [7:0] in_1,
  input  [7:0] in_2,
  input  [7:0] in_3,
  input  [7:0] in_4,
  input  [7:0] in_5,
  input  [7:0] in_6,
  input  [7:0] in_7,
  input  [7:0] in_8,
  input  [7:0] in_9,
  input  [7:0] in_10,
  input  [7:0] in_11,
  input  [7:0] in_12,
  input  [7:0] in_13,
  input  [7:0] in_14,
  input  [7:0] in_15,
  input  [7:0] in_16,
  output [7:0] out_17
);

  or or_1 (out_17[0], in_16[0], in_15[0], in_14[0], in_13[0], in_12[0], in_11[0], in_10[0], in_9[0], in_8[0], in_7[0], in_6[0], in_5[0], in_4[0], in_3[0], in_2[0], in_1[0]);
  or or_2 (out_17[1], in_16[1], in_15[1], in_14[1], in_13[1], in_12[1], in_11[1], in_10[1], in_9[1], in_8[1], in_7[1], in_6[1], in_5[1], in_4[1], in_3[1], in_2[1], in_1[1]);
  or or_3 (out_17[2], in_16[2], in_15[2], in_14[2], in_13[2], in_12[2], in_11[2], in_10[2], in_9[2], in_8[2], in_7[2], in_6[2], in_5[2], in_4[2], in_3[2], in_2[2], in_1[2]);
  or or_4 (out_17[3], in_16[3], in_15[3], in_14[3], in_13[3], in_12[3], in_11[3], in_10[3], in_9[3], in_8[3], in_7[3], in_6[3], in_5[3], in_4[3], in_3[3], in_2[3], in_1[3]);
  or or_5 (out_17[4], in_16[4], in_15[4], in_14[4], in_13[4], in_12[4], in_11[4], in_10[4], in_9[4], in_8[4], in_7[4], in_6[4], in_5[4], in_4[4], in_3[4], in_2[4], in_1[4]);
  or or_6 (out_17[5], in_16[5], in_15[5], in_14[5], in_13[5], in_12[5], in_11[5], in_10[5], in_9[5], in_8[5], in_7[5], in_6[5], in_5[5], in_4[5], in_3[5], in_2[5], in_1[5]);
  or or_7 (out_17[6], in_16[6], in_15[6], in_14[6], in_13[6], in_12[6], in_11[6], in_10[6], in_9[6], in_8[6], in_7[6], in_6[6], in_5[6], in_4[6], in_3[6], in_2[6], in_1[6]);
  or or_8 (out_17[7], in_16[7], in_15[7], in_14[7], in_13[7], in_12[7], in_11[7], in_10[7], in_9[7], in_8[7], in_7[7], in_6[7], in_5[7], in_4[7], in_3[7], in_2[7], in_1[7]);
endmodule

module \byte  (
  input  CLOCK,
  input  RW,
  input  EN,
  input  [7:0] InputBits,
  output [7:0] Outputbits
);

  wire and_1_out, and_2_out, and_3_out, and_4_out, and_5_out, and_6_out, and_7_out, and_8_out, and_9_out,
       and_10_out, not_1_out, not_2_out, not_3_out, not_4_out, not_5_out, not_6_out, not_7_out, not_8_out,
       not_9_out, s_r_ff_1_q, s_r_ff_2_q, s_r_ff_3_q, s_r_ff_4_q, s_r_ff_5_q, s_r_ff_6_q, s_r_ff_7_q,
       s_r_ff_8_q;

  and and_1 (and_1_out, CLOCK, RW, EN, InputBits[7]);
  and and_2 (and_2_out, CLOCK, RW, EN, InputBits[6]);
  and and_3 (and_3_out, CLOCK, RW, EN, InputBits[5]);
  and and_4 (and_4_out, CLOCK, RW, EN, InputBits[4]);
  and and_5 (and_5_out, CLOCK, RW, EN, InputBits[3]);
  and and_6 (and_6_out, CLOCK, EN, InputBits[2]);
  and and_7 (and_7_out, CLOCK, RW, EN, InputBits[1]);
  and and_8 (and_8_out, CLOCK, RW, EN, InputBits[0]);
  and and_9 (and_9_out, EN, RW, CLOCK);
  not not_1 (not_1_out, RW);
  and and_10 (and_10_out, EN, not_1_out, CLOCK);
  S_R_Flip_Flop #(.trigger("high")) s_r_ff_1 (
    .S(and_1_out), .clk(and_9_out), .R(not_2_out), .Q(s_r_ff_1_q));  // open: Qn, preset, reset, en
  not not_2 (not_2_out, and_1_out);
  S_R_Flip_Flop #(.trigger("high")) s_r_ff_2 (
    .S(and_2_out), .clk(and_9_out), .R(not_3_out), .Q(s_r_ff_2_q));  // open: Qn, preset, reset, en
  not not_3 (not_3_out, and_2_out);
  S_R_Flip_Flop #(.trigger("high")) s_r_ff_3 (
    .S(and_3_out), .clk(and_9_out), .R(not_4_out), .Q(s_r_ff_3_q));  // open: Qn, preset, reset, en
  not not_4 (not_4_out, and_3_out);
  S_R_Flip_Flop #(.trigger("high")) s_r_ff_4 (
    .S(and_4_out), .clk(and_9_out), .R(not_5_out), .Q(s_r_ff_4_q));  // open: Qn, preset, reset, en
  not not_5 (not_5_out, and_4_out);
  S_R_Flip_Flop #(.trigger("high")) s_r_ff_5 (
    .S(and_5_out), .clk(and_9_out), .R(not_6_out), .Q(s_r_ff_5_q));  // open: Qn, preset, reset, en
  not not_6 (not_6_out, and_5_out);
  S_R_Flip_Flop #(.trigger("high")) s_r_ff_6 (
    .S(and_6_out), .clk(and_9_out), .R(not_7_out), .Q(s_r_ff_6_q));  // open: Qn, preset, reset, en
  not not_7 (not_7_out, and_6_out);
  S_R_Flip_Flop #(.trigger("high")) s_r_ff_7 (
    .S(and_7_out), .clk(and_9_out), .R(not_8_out), .Q(s_r_ff_7_q));  // open: Qn, preset, reset, en
  not not_8 (not_8_out, and_7_out);
  S_R_Flip_Flop #(.trigger("high")) s_r_ff_8 (
    .S(and_8_out), .clk(and_9_out), .R(not_9_out), .Q(s_r_ff_8_q));  // open: Qn, preset, reset, en
  not not_9 (not_9_out, and_8_out);
  and and_11 (Outputbits[0], s_r_ff_1_q, and_10_out);
  and and_12 (Outputbits[1], s_r_ff_2_q, and_10_out);
  and and_13 (Outputbits[2], s_r_ff_3_q, and_10_out);
  and and_14 (Outputbits[3], s_r_ff_4_q, and_10_out);
  and and_15 (Outputbits[4], s_r_ff_5_q, and_10_out);
  and and_16 (Outputbits[5], s_r_ff_6_q, and_10_out);
  and and_17 (Outputbits[6], s_r_ff_7_q, and_10_out);
  and and_18 (Outputbits[7], s_r_ff_8_q, and_10_out);
endmodule

module CPU_project (
  input  [9:0] PINS_0_to_9,
  input  in_2,
  input  ENTER,
  input  [7:0] in_4,
  output [7:0] out_5
);

  wire display_1_a, display_1_b, display_1_c, display_1_d, display_1_e, display_1_f, display_1_g,
       display_2_a, display_2_b, display_2_c, display_2_d, display_2_e, display_2_f, display_2_g,
       display_3_a, display_3_b, display_3_c, display_3_d, display_3_e, display_3_f, display_3_g,
       registers_3_p2;
  wire [3:0] compressor_1_out_2, makingbdc_1_out_3, makingbdc_1_out_4, makingbdc_1_out_5;
  wire [7:0] undriven, undriven_2;

  registers registers_1 ();  // open: CLK, R_W, ENABLE, INPUT, out_5
  keypad_buttons_and_outputs keypad_buttons_and_outputs_1 (
    ._0(PINS_0_to_9[0]), ._1(PINS_0_to_9[1]), ._2(PINS_0_to_9[2]), ._3(PINS_0_to_9[3]), ._4(PINS_0_to_9[4]),
    ._5(PINS_0_to_9[5]), ._6(PINS_0_to_9[6]), ._7(PINS_0_to_9[7]), ._8(PINS_0_to_9[8]), ._9(PINS_0_to_9[9]),
    .ENTER(ENTER));  // open: out_12
  compressor compressor_1 (.in_1(undriven_2), .out_2(compressor_1_out_2));
  makingBDC makingbdc_1 (
    .in_2(in_4), .out_3(makingbdc_1_out_3), .out_4(makingbdc_1_out_4), .out_5(makingbdc_1_out_5));  // open: ENABLE
  RAM_project ram_project_1 (
    .DATA(undriven[0]), .in_8(undriven[1]), .in_9(undriven[2]), .in_10(undriven[3]), .in_11(undriven[4]),
    .in_12(undriven[5]), .in_13(undriven[6]), .in_14(undriven[7]), .ADDR(compressor_1_out_2[3]),
    .in_2(compressor_1_out_2[2]), .in_3(compressor_1_out_2[1]), .in_4(compressor_1_out_2[0]));  // open: RW, CLK, out_15
  registers registers_2 ();  // open: CLK, R_W, ENABLE, INPUT, out_5
  display display_1 (
    .d(display_1_d), .e(display_1_e), .g(display_1_g), .b(display_1_b), .a(display_1_a), .c(display_1_c),
    .f(display_1_f), .in_1(makingbdc_1_out_3));
  display display_2 (
    .d(display_2_d), .e(display_2_e), .g(display_2_g), .b(display_2_b), .a(display_2_a), .c(display_2_c),
    .f(display_2_f), .in_1(makingbdc_1_out_4));
  display display_3 (
    .d(display_3_d), .e(display_3_e), .g(display_3_g), .b(display_3_b), .a(display_3_a), .c(display_3_c),
    .f(display_3_f), .in_1(makingbdc_1_out_5));
  _7_Segment_Display u_7_segment_display_1 (
    .g(display_3_d), .f(display_3_b), .a(display_3_a), .b(display_3_c), .e(display_3_e), .d(display_3_g),
    .c(display_3_f));  // open: dp
  // registers registers_3: pin names not known; wires that end beside it: in_2, registers_3_p2, out_5
  _7_Segment_Display u_7_segment_display_2 (
    .g(display_2_d), .f(display_2_b), .a(display_2_a), .b(display_2_c), .e(display_2_e), .d(display_2_g),
    .c(display_2_f));  // open: dp
  _7_Segment_Display u_7_segment_display_3 (
    .g(display_1_d), .f(display_1_b), .a(display_1_a), .b(display_1_c), .e(display_1_e), .d(display_1_g),
    .c(display_1_f));  // open: dp
endmodule

module display (
  input  [3:0] in_1,
  output a,
  output b,
  output c,
  output d,
  output f,
  output e,
  output g
);

  wire _0_out, _1_out, _2_out, _3_out, _4_out, _5_out, _6_out, _7_out, _9_out, _10_plus_out, a_out,
       and_1_out, and_2_out, b_out, c_out, d_out, e_out, f_out, g_out, not_1_out, not_2_out, not_3_out,
       not_4_out, not_5_out, not_6_out, not_7_out, not_8_out, not_9_out, not_10_out, not_11_out, not_12_out,
       not_13_out, not_14_out, not_15_out, not_16_out, not_17_out, not_18_out, not_19_out, not_20_out,
       not_21_out, not_22_out;

  not not_1 (not_1_out, in_1[1]);
  not not_2 (not_2_out, in_1[2]);
  not not_3 (not_3_out, in_1[3]);
  not not_4 (not_4_out, in_1[0]);
  not not_5 (not_5_out, in_1[1]);
  not not_6 (not_6_out, in_1[3]);
  not not_7 (not_7_out, in_1[0]);
  not not_8 (not_8_out, in_1[2]);
  not not_9 (not_9_out, in_1[3]);
  not not_10 (not_10_out, in_1[2]);
  not not_11 (not_11_out, in_1[3]);
  not not_12 (not_12_out, in_1[3]);
  not not_13 (not_13_out, in_1[1]);
  not not_14 (not_14_out, in_1[3]);
  not not_15 (not_15_out, in_1[0]);
  not not_16 (not_16_out, in_1[3]);
  not not_17 (not_17_out, in_1[0]);
  not not_18 (not_18_out, in_1[1]);
  not not_19 (not_19_out, in_1[2]);
  not not_20 (not_20_out, in_1[3]);
  not not_21 (not_21_out, in_1[1]);
  not not_22 (not_22_out, in_1[2]);
  and and_1 (and_1_out, in_1[1], in_1[3]);
  and and_2 (and_2_out, in_1[2], in_1[3]);
  and _1 (_1_out, in_1[0], not_1_out, not_2_out, not_3_out);
  and _4 (_4_out, not_4_out, not_5_out, in_1[2], not_6_out);
  and _2 (_2_out, not_7_out, in_1[1], not_8_out, not_9_out);
  and _3 (_3_out, in_1[0], in_1[1], not_10_out, not_11_out);
  and _7 (_7_out, in_1[0], in_1[1], in_1[2], not_12_out);
  and _5 (_5_out, in_1[0], not_13_out, in_1[2], not_14_out);
  and _6 (_6_out, not_15_out, in_1[1], in_1[2], not_16_out);
  and _0 (_0_out, not_17_out, not_18_out, not_19_out, not_20_out);
  and _9 (_9_out, in_1[0], not_21_out, not_22_out, in_1[3]);
  or _10_plus (_10_plus_out, and_1_out, and_2_out);
  or u_a (a_out, _1_out, _4_out);
  or u_b (b_out, _1_out, _2_out, _3_out, _7_out);
  or u_c (c_out, _5_out, _10_plus_out, _6_out);
  or u_d (d_out, _7_out, _1_out, _0_out);
  or u_e (e_out, _1_out, _3_out, _4_out, _5_out, _7_out, _9_out);
  or u_f (f_out, _2_out, _10_plus_out);
  or u_g (g_out, _7_out, _4_out, _1_out);
  not not_23 (a, a_out);
  not not_24 (b, b_out);
  not not_25 (c, c_out);
  not not_26 (d, d_out);
  not not_27 (e, e_out);
  not not_28 (f, f_out);
  not not_29 (g, g_out);
endmodule

module decoder8to3_4s (
  input  in_1,
  input  in_2,
  input  in_3,
  input  in_4,
  output out_5,
  output out_6,
  output out_7,
  output out_8
);

  wire _0_out, _1_out, _2_out, _3_out, _4_out, _5_out, _6_out, _7_out, _8_out, _9_out, and_1_out, and_2_out,
       and_3_out, and_4_out, and_5_out, and_6_out, and_7_out, and_8_out, and_9_out, and_10_out, and_11_out,
       and_12_out, and_13_out, and_14_out, and_15_out, and_16_out, and_17_out, and_18_out, and_19_out,
       and_20_out, and_21_out, and_22_out, and_23_out, and_24_out, and_25_out, and_26_out, and_27_out,
       and_28_out, and_29_out, and_30_out, and_31_out, and_32_out, and_33_out, and_34_out, and_35_out,
       and_36_out, and_37_out, and_38_out, and_39_out, and_40_out, not_1_out, not_2_out, not_3_out,
       not_4_out, not_5_out, not_6_out, not_7_out, not_8_out, not_9_out, not_10_out, not_11_out, not_12_out,
       not_13_out, not_14_out, not_15_out, not_16_out, not_17_out, not_18_out, not_19_out, not_20_out,
       not_21_out, not_22_out, not_23_out, not_24_out, not_25_out, not_26_out, not_27_out, not_28_out,
       not_29_out, not_30_out, not_31_out, not_32_out, not_33_out, not_34_out, not_35_out, not_36_out,
       not_37_out, not_38_out, not_39_out, not_40_out, not_41_out, not_42_out, not_43_out, not_44_out,
       not_45_out, not_46_out, not_47_out, not_48_out, not_49_out, not_50_out;

  not not_1 (not_1_out, in_1);
  not not_2 (not_2_out, in_2);
  not not_3 (not_3_out, in_3);
  not not_4 (not_4_out, in_4);
  not not_5 (not_5_out, in_2);
  not not_6 (not_6_out, in_3);
  not not_7 (not_7_out, in_4);
  not not_8 (not_8_out, in_1);
  not not_9 (not_9_out, in_3);
  not not_10 (not_10_out, in_4);
  not not_11 (not_11_out, in_3);
  not not_12 (not_12_out, in_4);
  not not_13 (not_13_out, in_1);
  not not_14 (not_14_out, in_2);
  not not_15 (not_15_out, in_4);
  not not_16 (not_16_out, in_2);
  not not_17 (not_17_out, in_4);
  not not_18 (not_18_out, in_1);
  not not_19 (not_19_out, in_4);
  not not_20 (not_20_out, in_4);
  not not_21 (not_21_out, in_1);
  not not_22 (not_22_out, in_2);
  not not_23 (not_23_out, in_3);
  not not_24 (not_24_out, in_2);
  not not_25 (not_25_out, in_3);
  and _0 (_0_out, not_1_out, not_2_out, not_3_out, not_4_out);
  and _1 (_1_out, in_1, not_5_out, not_6_out, not_7_out);
  and _2 (_2_out, not_8_out, in_2, not_9_out, not_10_out);
  and _3 (_3_out, in_1, in_2, not_11_out, not_12_out);
  and _4 (_4_out, not_13_out, not_14_out, in_3, not_15_out);
  and _5 (_5_out, in_1, not_16_out, in_3, not_17_out);
  and _6 (_6_out, not_18_out, in_2, in_3, not_19_out);
  and _7 (_7_out, in_1, in_2, in_3, not_20_out);
  and _8 (_8_out, not_21_out, not_22_out, not_23_out, in_4);
  and _9 (_9_out, in_1, not_24_out, not_25_out, in_4);
  not not_26 (not_26_out, _0_out);
  not not_27 (not_27_out, _0_out);
  not not_28 (not_28_out, _0_out);
  not not_29 (not_29_out, _0_out);
  not not_30 (not_30_out, _1_out);
  not not_31 (not_31_out, _1_out);
  not not_32 (not_32_out, _1_out);
  not not_33 (not_33_out, _2_out);
  not not_34 (not_34_out, _2_out);
  not not_35 (not_35_out, _2_out);
  not not_36 (not_36_out, _3_out);
  not not_37 (not_37_out, _3_out);
  not not_38 (not_38_out, _4_out);
  not not_39 (not_39_out, _4_out);
  not not_40 (not_40_out, _4_out);
  not not_41 (not_41_out, _5_out);
  not not_42 (not_42_out, _5_out);
  not not_43 (not_43_out, _5_out);
  not not_44 (not_44_out, _6_out);
  not not_45 (not_45_out, _6_out);
  not not_46 (not_46_out, _7_out);
  not not_47 (not_47_out, _7_out);
  not not_48 (not_48_out, _8_out);
  not not_49 (not_49_out, _9_out);
  not not_50 (not_50_out, _9_out);
  and and_1 (and_1_out, not_26_out, _0_out);
  and and_2 (and_2_out, not_27_out, _0_out);
  and and_3 (and_3_out, not_28_out, _0_out);
  and and_4 (and_4_out, not_29_out, _0_out);
  and and_5 (and_5_out, _1_out, _1_out);
  and and_6 (and_6_out, not_30_out, _1_out);
  and and_7 (and_7_out, not_31_out, _1_out);
  and and_8 (and_8_out, not_32_out, _1_out);
  and and_9 (and_9_out, not_33_out, _2_out);
  and and_10 (and_10_out, _2_out, _2_out);
  and and_11 (and_11_out, not_34_out, _2_out);
  and and_12 (and_12_out, not_35_out, _2_out);
  and and_13 (and_13_out, _3_out, _3_out);
  and and_14 (and_14_out, _3_out, _3_out);
  and and_15 (and_15_out, not_36_out, _3_out);
  and and_16 (and_16_out, not_37_out, _3_out);
  and and_17 (and_17_out, not_38_out, _4_out);
  and and_18 (and_18_out, not_39_out, _4_out);
  and and_19 (and_19_out, _4_out, _4_out);
  and and_20 (and_20_out, not_40_out, _4_out);
  and and_21 (and_21_out, not_41_out, _5_out);
  and and_22 (and_22_out, not_42_out, _5_out);
  and and_23 (and_23_out, not_43_out, _5_out);
  and and_24 (and_24_out, _5_out, _5_out);
  and and_25 (and_25_out, _6_out, _6_out);
  and and_26 (and_26_out, not_44_out, _6_out);
  and and_27 (and_27_out, not_45_out, _6_out);
  and and_28 (and_28_out, _6_out, _6_out);
  and and_29 (and_29_out, not_46_out, _7_out);
  and and_30 (and_30_out, _7_out, _7_out);
  and and_31 (and_31_out, not_47_out, _7_out);
  and and_32 (and_32_out, _7_out, _7_out);
  and and_33 (and_33_out, _8_out, _8_out);
  and and_34 (and_34_out, _8_out, _8_out);
  and and_35 (and_35_out, not_48_out, _8_out);
  and and_36 (and_36_out, _8_out, _8_out);
  and and_37 (and_37_out, not_49_out, _9_out);
  and and_38 (and_38_out, not_50_out, _9_out);
  and and_39 (and_39_out, _9_out, _9_out);
  and and_40 (and_40_out, _9_out, _9_out);
  or or_1 (out_8, and_1_out, and_5_out, and_9_out, and_13_out, and_17_out, and_21_out, and_25_out, and_29_out, and_33_out, and_37_out);
  or or_2 (out_7, and_2_out, and_6_out, and_10_out, and_14_out, and_18_out, and_22_out, and_26_out, and_30_out, and_34_out, and_38_out);
  or or_3 (out_6, and_3_out, and_7_out, and_11_out, and_15_out, and_19_out, and_23_out, and_27_out, and_31_out, and_35_out, and_39_out);
  or or_4 (out_5, and_4_out, and_8_out, and_12_out, and_16_out, and_20_out, and_24_out, and_28_out, and_32_out, and_36_out, and_40_out);
endmodule

module makingBDC (
  input  ENABLE,
  input  [7:0] in_2,
  output [3:0] out_3,
  output [3:0] out_4,
  output [3:0] out_5
);

  wire and_2_out, and_3_out, and_4_out, and_5_out, and_6_out, and_7_out, and_8_out, decoder8to3_4s_1_out_5,
       decoder8to3_4s_1_out_6, decoder8to3_4s_1_out_7, decoder8to3_4s_1_out_8, decoder8to3_4s_2_out_5,
       decoder8to3_4s_2_out_6, decoder8to3_4s_2_out_7, decoder8to3_4s_2_out_8, decoder8to3_4s_3_out_5,
       decoder8to3_4s_3_out_6, decoder8to3_4s_3_out_7, decoder8to3_4s_3_out_8, decoder8to3_4s_4_out_6,
       decoder8to3_4s_4_out_7, decoder8to3_4s_4_out_8, decoder8to3_4s_6_out_5, decoder8to3_4s_6_out_6,
       decoder8to3_4s_6_out_7, decoder8to3_4s_6_out_8;

  and and_1 (out_3[0], in_2[0], ENABLE);
  and and_2 (and_2_out, in_2[1], ENABLE);
  and and_3 (and_3_out, in_2[2], ENABLE);
  and and_4 (and_4_out, in_2[3], ENABLE);
  and and_5 (and_5_out, in_2[4], ENABLE);
  and and_6 (and_6_out, in_2[5], ENABLE);
  and and_7 (and_7_out, in_2[6], ENABLE);
  and and_8 (and_8_out, in_2[7], ENABLE);
  decoder8to3_4s decoder8to3_4s_1 (
    .in_1(and_6_out), .in_2(and_7_out), .out_5(decoder8to3_4s_1_out_5), .in_3(and_8_out),
    .out_6(decoder8to3_4s_1_out_6), .in_4(1'b0), .out_7(decoder8to3_4s_1_out_7),
    .out_8(decoder8to3_4s_1_out_8));
  decoder8to3_4s decoder8to3_4s_2 (
    .in_1(and_5_out), .in_2(decoder8to3_4s_1_out_8), .out_5(decoder8to3_4s_2_out_5),
    .in_3(decoder8to3_4s_1_out_7), .out_6(decoder8to3_4s_2_out_6), .in_4(decoder8to3_4s_1_out_6),
    .out_7(decoder8to3_4s_2_out_7), .out_8(decoder8to3_4s_2_out_8));
  decoder8to3_4s decoder8to3_4s_3 (
    .in_1(and_4_out), .in_2(decoder8to3_4s_2_out_8), .out_5(decoder8to3_4s_3_out_5),
    .in_3(decoder8to3_4s_2_out_7), .out_6(decoder8to3_4s_3_out_6), .in_4(decoder8to3_4s_2_out_6),
    .out_7(decoder8to3_4s_3_out_7), .out_8(decoder8to3_4s_3_out_8));
  decoder8to3_4s decoder8to3_4s_4 (
    .in_1(decoder8to3_4s_3_out_5), .in_2(decoder8to3_4s_2_out_5), .out_5(out_5[1]),
    .in_3(decoder8to3_4s_1_out_5), .out_6(decoder8to3_4s_4_out_6), .in_4(1'b0),
    .out_7(decoder8to3_4s_4_out_7), .out_8(decoder8to3_4s_4_out_8));
  decoder8to3_4s decoder8to3_4s_5 (
    .in_1(decoder8to3_4s_6_out_5), .in_2(decoder8to3_4s_4_out_8), .out_5(out_5[0]),
    .in_3(decoder8to3_4s_4_out_7), .out_6(out_4[3]), .in_4(decoder8to3_4s_4_out_6), .out_7(out_4[2]),
    .out_8(out_4[1]));
  decoder8to3_4s decoder8to3_4s_6 (
    .in_1(and_3_out), .in_2(decoder8to3_4s_3_out_8), .out_5(decoder8to3_4s_6_out_5),
    .in_3(decoder8to3_4s_3_out_7), .out_6(decoder8to3_4s_6_out_6), .in_4(decoder8to3_4s_3_out_6),
    .out_7(decoder8to3_4s_6_out_7), .out_8(decoder8to3_4s_6_out_8));
  decoder8to3_4s decoder8to3_4s_7 (
    .in_1(and_2_out), .in_2(decoder8to3_4s_6_out_8), .out_5(out_4[0]), .in_3(decoder8to3_4s_6_out_7),
    .out_6(out_3[3]), .in_4(decoder8to3_4s_6_out_6), .out_7(out_3[2]), .out_8(out_3[1]));

  assign out_5[3:2] = 2'b00;
endmodule

module keypad_buttons_and_outputs (
  input  _0,
  input  _1,
  input  _2,
  input  _3,
  input  _4,
  input  _5,
  input  _6,
  input  _7,
  input  _8,
  input  _9,
  input  ENTER,
  output [7:0] out_12
);

  wire and_1_out, and_2_out, and_3_out, and_4_out, and_5_out, and_6_out, and_7_out, and_8_out, and_9_out,
       and_10_out, only_one_pin_on_1_out_11, or_1_out, or_2_out, or_3_out, or_4_out;

  and and_1 (and_1_out, _0, 1'b1);
  and and_2 (and_2_out, _1, 1'b1);
  and and_3 (and_3_out, _2, 1'b1);
  and and_4 (and_4_out, _3, 1'b1);
  and and_5 (and_5_out, _4, 1'b1);
  and and_6 (and_6_out, _5, 1'b1);
  and and_7 (and_7_out, _6, 1'b1);
  and and_8 (and_8_out, _7, 1'b1);
  and and_9 (and_9_out, _8, 1'b1);
  and and_10 (and_10_out, _9, 1'b1);
  only_one_pin_on only_one_pin_on_1 (
    .in_1(and_1_out), .out_11(only_one_pin_on_1_out_11), .in_2(and_2_out), .in_3(and_3_out),
    .in_4(and_4_out), .in_5(and_5_out), .in_6(and_6_out), .in_7(and_7_out), .in_8(and_8_out),
    .in_9(and_9_out), .in_10(and_10_out));
  or or_1 (or_1_out, 1'b0, and_2_out, 1'b0, and_4_out, 1'b0, and_6_out, 1'b0, and_8_out, 1'b0, and_10_out);
  and and_11 (out_12[0], or_1_out, only_one_pin_on_1_out_11, ENTER);
  or or_2 (or_2_out, 1'b0, 1'b0, and_3_out, and_4_out, 1'b0, 1'b0, and_7_out, and_8_out, 1'b0, 1'b0);
  and and_12 (out_12[1], or_2_out, only_one_pin_on_1_out_11, ENTER);
  or or_3 (or_3_out, 1'b0, 1'b0, 1'b0, 1'b0, and_5_out, and_6_out, and_7_out, and_8_out, 1'b0, 1'b0);
  and and_13 (out_12[2], or_3_out, only_one_pin_on_1_out_11, ENTER);
  or or_4 (or_4_out, 1'b0, 1'b0, 1'b0, 1'b0, 1'b0, 1'b0, 1'b0, 1'b0, and_9_out, and_10_out);
  and and_14 (out_12[3], or_4_out, only_one_pin_on_1_out_11, ENTER);

  assign out_12[7:4] = 4'b0000;
endmodule

module keypad_buffer (
  input  ENTER,
  input  [7:0] in_2,
  output [7:0] out_3
);

  D_Flip_Flop d_ff_1 (.clk(ENTER), .D(in_2[0]), .Q(out_3[0]));  // open: Qn, preset, en, reset
  D_Flip_Flop d_ff_2 (.clk(ENTER), .D(in_2[1]), .Q(out_3[1]));  // open: Qn, preset, en, reset
  D_Flip_Flop d_ff_3 (.clk(ENTER), .D(in_2[2]), .Q(out_3[2]));  // open: Qn, preset, en, reset
  D_Flip_Flop d_ff_4 (.clk(ENTER), .D(in_2[3]), .Q(out_3[3]));  // open: Qn, preset, en, reset
  D_Flip_Flop d_ff_5 (.clk(ENTER), .D(in_2[4]), .Q(out_3[4]));  // open: Qn, preset, en, reset
  D_Flip_Flop d_ff_6 (.clk(ENTER), .D(in_2[5]), .Q(out_3[5]));  // open: Qn, preset, en, reset
  D_Flip_Flop d_ff_7 (.clk(ENTER), .D(in_2[6]), .Q(out_3[6]));  // open: Qn, preset, en, reset
  D_Flip_Flop d_ff_8 (.clk(ENTER), .D(in_2[7]), .Q(out_3[7]));  // open: Qn, preset, en, reset
endmodule

module registers (
  input  CLK,
  input  R_W,
  input  ENABLE,
  input  [7:0] INPUT,
  output [7:0] out_5
);

  wire and_1_out, and_2_out, and_3_out, and_4_out, and_5_out, and_6_out, and_7_out, and_8_out, and_9_out,
       and_10_out, not_1_out, not_2_out, not_3_out, not_4_out, not_5_out, not_6_out, not_7_out, not_8_out,
       not_9_out, s_r_ff_1_q, s_r_ff_2_q, s_r_ff_3_q, s_r_ff_4_q, s_r_ff_5_q, s_r_ff_6_q, s_r_ff_7_q,
       s_r_ff_8_q;

  and and_1 (and_1_out, CLK, ENABLE);
  and and_2 (and_2_out, CLK, R_W, ENABLE);
  and and_3 (and_3_out, INPUT[0], CLK, R_W);
  not not_1 (not_1_out, and_3_out);
  and and_4 (and_4_out, INPUT[1], CLK, R_W);
  not not_2 (not_2_out, and_4_out);
  and and_5 (and_5_out, INPUT[2], CLK, R_W);
  not not_3 (not_3_out, and_5_out);
  and and_6 (and_6_out, INPUT[3], CLK, R_W);
  not not_4 (not_4_out, and_6_out);
  and and_7 (and_7_out, INPUT[4], CLK, R_W);
  not not_5 (not_5_out, and_7_out);
  and and_8 (and_8_out, INPUT[5], CLK, R_W);
  not not_6 (not_6_out, and_8_out);
  and and_9 (and_9_out, INPUT[6], CLK, R_W);
  not not_7 (not_7_out, and_9_out);
  and and_10 (and_10_out, INPUT[7], CLK, R_W);
  not not_8 (not_8_out, and_10_out);
  not not_9 (not_9_out, R_W);
  S_R_Flip_Flop #(.trigger("high")) s_r_ff_1 (
    .S(and_3_out), .clk(and_2_out), .R(not_1_out), .Q(s_r_ff_1_q));  // open: Qn, preset, reset, en
  S_R_Flip_Flop #(.trigger("high")) s_r_ff_2 (
    .S(and_4_out), .clk(and_2_out), .R(not_2_out), .Q(s_r_ff_2_q));  // open: Qn, preset, reset, en
  S_R_Flip_Flop #(.trigger("high")) s_r_ff_3 (
    .S(and_5_out), .clk(and_2_out), .R(not_3_out), .Q(s_r_ff_3_q));  // open: Qn, preset, reset, en
  S_R_Flip_Flop #(.trigger("high")) s_r_ff_4 (
    .S(and_6_out), .clk(and_2_out), .R(not_4_out), .Q(s_r_ff_4_q));  // open: Qn, preset, reset, en
  S_R_Flip_Flop #(.trigger("high")) s_r_ff_5 (
    .S(and_7_out), .clk(and_2_out), .R(not_5_out), .Q(s_r_ff_5_q));  // open: Qn, preset, reset, en
  S_R_Flip_Flop #(.trigger("high")) s_r_ff_6 (
    .S(and_8_out), .clk(and_2_out), .R(not_6_out), .Q(s_r_ff_6_q));  // open: Qn, preset, reset, en
  S_R_Flip_Flop #(.trigger("high")) s_r_ff_7 (
    .S(and_9_out), .clk(and_2_out), .R(not_7_out), .Q(s_r_ff_7_q));  // open: Qn, preset, reset, en
  S_R_Flip_Flop #(.trigger("high")) s_r_ff_8 (
    .S(and_10_out), .clk(and_2_out), .R(not_8_out), .Q(s_r_ff_8_q));  // open: Qn, preset, reset, en
  and and_11 (out_5[0], s_r_ff_1_q, and_1_out, not_9_out);
  and and_12 (out_5[1], s_r_ff_2_q, and_1_out, not_9_out);
  and and_13 (out_5[2], s_r_ff_3_q, and_1_out, not_9_out);
  and and_14 (out_5[3], s_r_ff_4_q, and_1_out, not_9_out);
  and and_15 (out_5[4], s_r_ff_5_q, and_1_out, not_9_out);
  and and_16 (out_5[5], s_r_ff_6_q, and_1_out, not_9_out);
  and and_17 (out_5[6], s_r_ff_7_q, and_1_out, not_9_out);
  and and_18 (out_5[7], s_r_ff_8_q, and_1_out, not_9_out);
endmodule

module only_one_pin_on (
  input  in_1,
  input  in_2,
  input  in_3,
  input  in_4,
  input  in_5,
  input  in_6,
  input  in_7,
  input  in_8,
  input  in_9,
  input  in_10,
  output out_11
);

  wire and_1_out, and_2_out, and_3_out, and_4_out, and_5_out, and_6_out, and_7_out, and_8_out, and_9_out,
       and_10_out, not_1_out, not_2_out, not_3_out, not_4_out, not_5_out, not_6_out, not_7_out, not_8_out,
       not_9_out, not_10_out, or_1_out, or_2_out, or_3_out, or_4_out, or_5_out, or_6_out, or_7_out, or_8_out,
       or_9_out, or_10_out;

  or or_1 (or_1_out, in_2, in_3, in_4, in_5, in_6, in_7, in_8, in_9, in_10);
  and and_1 (and_1_out, in_1, not_1_out);
  not not_1 (not_1_out, or_1_out);
  not not_2 (not_2_out, or_2_out);
  or or_2 (or_2_out, in_1, in_3, in_4, in_5, in_6, in_7, in_8, in_9, in_10);
  not not_3 (not_3_out, or_3_out);
  or or_3 (or_3_out, in_1, in_2, in_4, in_5, in_6, in_7, in_8, in_9, in_10);
  not not_4 (not_4_out, or_4_out);
  or or_4 (or_4_out, in_1, in_2, in_3, in_5, in_6, in_7, in_8, in_9, in_10);
  not not_5 (not_5_out, or_5_out);
  or or_5 (or_5_out, in_1, in_2, in_3, in_4, in_6, in_7, in_8, in_9, in_10);
  not not_6 (not_6_out, or_6_out);
  or or_6 (or_6_out, in_1, in_2, in_3, in_4, in_5, in_7, in_8, in_9, in_10);
  not not_7 (not_7_out, or_7_out);
  or or_7 (or_7_out, in_1, in_2, in_3, in_4, in_5, in_6, in_8, in_9, in_10);
  not not_8 (not_8_out, or_8_out);
  or or_8 (or_8_out, in_1, in_2, in_3, in_4, in_5, in_6, in_7, in_9, in_10);
  or or_9 (or_9_out, in_1, in_2, in_3, in_4, in_5, in_6, in_7, in_8, in_10);
  or or_10 (or_10_out, in_1, in_2, in_3, in_4, in_5, in_6, in_7, in_8, in_9);
  and and_2 (and_2_out, in_2, not_2_out);
  and and_3 (and_3_out, in_3, not_3_out);
  and and_4 (and_4_out, in_4, not_4_out);
  and and_5 (and_5_out, in_5, not_5_out);
  and and_6 (and_6_out, in_6, not_6_out);
  and and_7 (and_7_out, in_7, not_7_out);
  and and_8 (and_8_out, in_8, not_8_out);
  and and_9 (and_9_out, in_9, not_9_out);
  not not_9 (not_9_out, or_9_out);
  and and_10 (and_10_out, in_10, not_10_out);
  not not_10 (not_10_out, or_10_out);
  or or_11 (out_11, and_1_out, and_2_out, and_3_out, and_4_out, and_5_out, and_6_out, and_7_out, and_8_out, and_9_out, and_10_out);
endmodule

module compressor (
  input  [7:0] in_1,
  output [3:0] out_2
);


  assign out_2 = in_1[3:0];
endmodule

module ALU (
  input  in_1,
  input  in_2,
  input  [7:0] in_3,
  input  [7:0] in_4,
  input  in_5,
  output Overflow,
  output Zero,
  output Negative,
  output [7:0] out_9
);

  wire and_1_out, and_2_out, and_3_out, and_4_out, and_5_out, and_6_out, and_7_out, and_8_out, and_17_out,
       and_18_out, and_19_out, and_20_out, and_21_out, and_22_out, and_23_out, and_24_out, and_25_out,
       and_26_out, and_27_out, and_28_out, and_29_out, and_30_out, and_31_out, and_32_out,
       full_adder_1_out_4, full_adder_1_out_5, full_adder_2_out_4, full_adder_2_out_5, full_adder_3_out_4,
       full_adder_3_out_5, full_adder_4_out_4, full_adder_4_out_5, full_adder_5_out_4, full_adder_5_out_5,
       full_adder_6_out_4, full_adder_6_out_5, full_adder_7_out_4, full_adder_7_out_5, half_adder_1_out_3,
       half_adder_1_out_4, not_1_out, not_2_out, not_3_out, not_4_out, not_5_out, not_6_out, not_7_out,
       not_8_out, not_9_out, or_1_out, or_3_out, xor_1_out;
  wire [7:0] alu2c_1_out_3, and_9_out;
  wire [15:0] adder_1_out, adder_2_out, adder_3_out, adder_4_out, adder_5_out, adder_6_out, adder_7_out,
       adder_8_out, multhelper_1_out_3, multhelper_2_out_3, multhelper_3_out_3, multhelper_4_out_3,
       multhelper_5_out_3, multhelper_6_out_3, multhelper_7_out_3, multhelper_8_out_3, n16bitshift_1_out_2,
       n16bitshift_2_out_2, n16bitshift_3_out_2, n16bitshift_4_out_2, n16bitshift_5_out_2,
       n16bitshift_6_out_2, n16bitshift_7_out_2, n16bitshift_8_out_2, n16bitshift_9_out_2,
       n16bitshift_10_out_2, n16bitshift_11_out_2, n16bitshift_12_out_2, n16bitshift_13_out_2,
       n16bitshift_14_out_2, n16bitshift_15_out_2, n16bitshift_16_out_2, n16bitshift_17_out_2,
       n16bitshift_18_out_2, n16bitshift_19_out_2, n16bitshift_20_out_2, n16bitshift_21_out_2,
       n16bitshift_22_out_2, n16bitshift_23_out_2, n16bitshift_24_out_2, n16bitshift_25_out_2,
       n16bitshift_26_out_2, n16bitshift_27_out_2, n16bitshift_28_out_2;

  and and_1 (and_1_out, in_3[0], in_5);
  and and_2 (and_2_out, in_3[1], in_5);
  and and_3 (and_3_out, in_3[2], in_5);
  and and_4 (and_4_out, in_3[3], in_5);
  and and_5 (and_5_out, in_3[4], in_5);
  and and_6 (and_6_out, in_3[5], in_5);
  and and_7 (and_7_out, in_3[6], in_5);
  and and_8 (and_8_out, in_3[7], in_5);
  and and_9 (and_9_out[0], in_4[0], in_5);
  and and_10 (and_9_out[1], in_4[1], in_5);
  and and_11 (and_9_out[2], in_4[2], in_5);
  and and_12 (and_9_out[3], in_4[3], in_5);
  and and_13 (and_9_out[4], in_4[4], in_5);
  and and_14 (and_9_out[5], in_4[5], in_5);
  and and_15 (and_9_out[6], in_4[6], in_5);
  and and_16 (and_9_out[7], in_4[7], in_5);
  ALU2C alu2c_1 (.in_1(in_2), .in_2(in_4), .out_3(alu2c_1_out_3));
  or or_1 (or_1_out, in_1, in_2);
  multhelper multhelper_1 (.in_1({{8{1'b0}}, and_9_out}), .out_3(multhelper_1_out_3), .in_2(and_1_out));
  and and_17 (and_17_out, in_3[0], or_1_out);
  and and_18 (and_18_out, in_3[1], or_1_out);
  and and_19 (and_19_out, in_3[2], or_1_out);
  and and_20 (and_20_out, in_3[3], or_1_out);
  and and_21 (and_21_out, in_3[4], or_1_out);
  and and_22 (and_22_out, in_3[5], or_1_out);
  and and_23 (and_23_out, in_3[6], or_1_out);
  and and_24 (and_24_out, in_3[7], or_1_out);
  and and_25 (and_25_out, alu2c_1_out_3[0], or_1_out);
  and and_26 (and_26_out, alu2c_1_out_3[1], or_1_out);
  and and_27 (and_27_out, alu2c_1_out_3[2], or_1_out);
  and and_28 (and_28_out, alu2c_1_out_3[3], or_1_out);
  and and_29 (and_29_out, alu2c_1_out_3[4], or_1_out);
  and and_30 (and_30_out, alu2c_1_out_3[5], or_1_out);
  and and_31 (and_31_out, alu2c_1_out_3[6], or_1_out);
  and and_32 (and_32_out, alu2c_1_out_3[7], or_1_out);
  Adder #(.width(16)) adder_1 (.a(multhelper_1_out_3), .b({16{1'b0}}), .out(adder_1_out));  // open: cin, cout
  multhelper multhelper_2 (.in_1({{8{1'b0}}, and_9_out}), .out_3(multhelper_2_out_3), .in_2(and_2_out));
  _16bitshift u_16bitshift_1 (.in_1(multhelper_2_out_3), .out_2(n16bitshift_1_out_2));
  Adder #(.width(16)) adder_2 (.a(n16bitshift_1_out_2), .b(adder_1_out), .out(adder_2_out));  // open: cin, cout
  multhelper multhelper_3 (.in_1({{8{1'b0}}, and_9_out}), .out_3(multhelper_3_out_3), .in_2(and_3_out));
  _16bitshift u_16bitshift_2 (.in_1(multhelper_3_out_3), .out_2(n16bitshift_2_out_2));
  _16bitshift u_16bitshift_3 (.in_1(n16bitshift_2_out_2), .out_2(n16bitshift_3_out_2));
  Adder #(.width(16)) adder_3 (.a(n16bitshift_3_out_2), .b(adder_2_out), .out(adder_3_out));  // open: cin, cout
  multhelper multhelper_4 (.in_1({{8{1'b0}}, and_9_out}), .out_3(multhelper_4_out_3), .in_2(and_4_out));
  _16bitshift u_16bitshift_4 (.in_1(multhelper_4_out_3), .out_2(n16bitshift_4_out_2));
  _16bitshift u_16bitshift_5 (.in_1(n16bitshift_4_out_2), .out_2(n16bitshift_5_out_2));
  _16bitshift u_16bitshift_6 (.in_1(n16bitshift_5_out_2), .out_2(n16bitshift_6_out_2));
  Adder #(.width(16)) adder_4 (.a(n16bitshift_6_out_2), .b(adder_3_out), .out(adder_4_out));  // open: cin, cout
  half_adder half_adder_1 (
    .in_1(and_17_out), .in_2(and_25_out), .out_3(half_adder_1_out_3), .out_4(half_adder_1_out_4));
  full_adder full_adder_1 (
    .in_2(and_18_out), .in_3(and_26_out), .out_4(full_adder_1_out_4), .in_1(half_adder_1_out_4),
    .out_5(full_adder_1_out_5));
  full_adder full_adder_2 (
    .in_2(and_19_out), .in_3(and_27_out), .out_4(full_adder_2_out_4), .in_1(full_adder_1_out_5),
    .out_5(full_adder_2_out_5));
  full_adder full_adder_3 (
    .in_2(and_20_out), .in_3(and_28_out), .out_4(full_adder_3_out_4), .in_1(full_adder_2_out_5),
    .out_5(full_adder_3_out_5));
  full_adder full_adder_4 (
    .in_2(and_21_out), .in_3(and_29_out), .out_4(full_adder_4_out_4), .in_1(full_adder_3_out_5),
    .out_5(full_adder_4_out_5));
  full_adder full_adder_5 (
    .in_2(and_22_out), .in_3(and_30_out), .out_4(full_adder_5_out_4), .in_1(full_adder_4_out_5),
    .out_5(full_adder_5_out_5));
  full_adder full_adder_6 (
    .in_2(and_23_out), .in_3(and_31_out), .out_4(full_adder_6_out_4), .in_1(full_adder_5_out_5),
    .out_5(full_adder_6_out_5));
  full_adder full_adder_7 (
    .in_2(and_24_out), .in_3(and_32_out), .out_4(full_adder_7_out_4), .in_1(full_adder_6_out_5),
    .out_5(full_adder_7_out_5));
  multhelper multhelper_5 (.in_1({{8{1'b0}}, and_9_out}), .out_3(multhelper_5_out_3), .in_2(and_5_out));
  _16bitshift u_16bitshift_7 (.in_1(multhelper_5_out_3), .out_2(n16bitshift_7_out_2));
  _16bitshift u_16bitshift_8 (.in_1(n16bitshift_7_out_2), .out_2(n16bitshift_8_out_2));
  _16bitshift u_16bitshift_9 (.in_1(n16bitshift_8_out_2), .out_2(n16bitshift_9_out_2));
  _16bitshift u_16bitshift_10 (.in_1(n16bitshift_9_out_2), .out_2(n16bitshift_10_out_2));
  Adder #(.width(16)) adder_5 (.a(n16bitshift_10_out_2), .b(adder_4_out), .out(adder_5_out));  // open: cin, cout
  xor xor_1 (xor_1_out, full_adder_6_out_5, full_adder_7_out_5);
  multhelper multhelper_6 (.in_1({{8{1'b0}}, and_9_out}), .out_3(multhelper_6_out_3), .in_2(and_6_out));
  _16bitshift u_16bitshift_11 (.in_1(multhelper_6_out_3), .out_2(n16bitshift_11_out_2));
  _16bitshift u_16bitshift_12 (.in_1(n16bitshift_11_out_2), .out_2(n16bitshift_12_out_2));
  _16bitshift u_16bitshift_13 (.in_1(n16bitshift_12_out_2), .out_2(n16bitshift_13_out_2));
  _16bitshift u_16bitshift_14 (.in_1(n16bitshift_13_out_2), .out_2(n16bitshift_14_out_2));
  _16bitshift u_16bitshift_15 (.in_1(n16bitshift_14_out_2), .out_2(n16bitshift_15_out_2));
  Adder #(.width(16)) adder_6 (.a(n16bitshift_15_out_2), .b(adder_5_out), .out(adder_6_out));  // open: cin, cout
  multhelper multhelper_7 (.in_1({{8{1'b0}}, and_9_out}), .out_3(multhelper_7_out_3), .in_2(and_7_out));
  _16bitshift u_16bitshift_16 (.in_1(multhelper_7_out_3), .out_2(n16bitshift_16_out_2));
  _16bitshift u_16bitshift_17 (.in_1(n16bitshift_16_out_2), .out_2(n16bitshift_17_out_2));
  _16bitshift u_16bitshift_18 (.in_1(n16bitshift_17_out_2), .out_2(n16bitshift_18_out_2));
  _16bitshift u_16bitshift_19 (.in_1(n16bitshift_18_out_2), .out_2(n16bitshift_19_out_2));
  _16bitshift u_16bitshift_20 (.in_1(n16bitshift_19_out_2), .out_2(n16bitshift_20_out_2));
  _16bitshift u_16bitshift_21 (.in_1(n16bitshift_20_out_2), .out_2(n16bitshift_21_out_2));
  Adder #(.width(16)) adder_7 (.a(n16bitshift_21_out_2), .b(adder_6_out), .out(adder_7_out));  // open: cin, cout
  multhelper multhelper_8 (.in_1({{8{1'b0}}, and_9_out}), .out_3(multhelper_8_out_3), .in_2(and_8_out));
  _16bitshift u_16bitshift_22 (.in_1(multhelper_8_out_3), .out_2(n16bitshift_22_out_2));
  _16bitshift u_16bitshift_23 (.in_1(n16bitshift_22_out_2), .out_2(n16bitshift_23_out_2));
  _16bitshift u_16bitshift_24 (.in_1(n16bitshift_23_out_2), .out_2(n16bitshift_24_out_2));
  _16bitshift u_16bitshift_25 (.in_1(n16bitshift_24_out_2), .out_2(n16bitshift_25_out_2));
  _16bitshift u_16bitshift_26 (.in_1(n16bitshift_25_out_2), .out_2(n16bitshift_26_out_2));
  _16bitshift u_16bitshift_27 (.in_1(n16bitshift_26_out_2), .out_2(n16bitshift_27_out_2));
  _16bitshift u_16bitshift_28 (.in_1(n16bitshift_27_out_2), .out_2(n16bitshift_28_out_2));
  Adder #(.width(16)) adder_8 (.a(n16bitshift_28_out_2), .b(adder_7_out), .out(adder_8_out));  // open: cin, cout
  not not_1 (not_1_out, Overflow);
  and and_33 (Negative, not_1_out, out_9[7]);
  or or_2 (Overflow, or_3_out, xor_1_out);
  or or_3 (or_3_out, adder_8_out[8], adder_8_out[9], adder_8_out[10], adder_8_out[11], adder_8_out[12], adder_8_out[13], adder_8_out[14], adder_8_out[15]);
  or or_4 (out_9[0], half_adder_1_out_3, adder_8_out[0]);
  or or_5 (out_9[1], full_adder_1_out_4, adder_8_out[1]);
  or or_6 (out_9[2], full_adder_2_out_4, adder_8_out[2]);
  or or_7 (out_9[3], full_adder_3_out_4, adder_8_out[3]);
  or or_8 (out_9[4], full_adder_4_out_4, adder_8_out[4]);
  or or_9 (out_9[5], full_adder_5_out_4, adder_8_out[5]);
  or or_10 (out_9[6], full_adder_6_out_4, adder_8_out[6]);
  or or_11 (out_9[7], full_adder_7_out_4, adder_8_out[7]);
  not not_2 (not_2_out, out_9[1]);
  not not_3 (not_3_out, out_9[0]);
  not not_4 (not_4_out, out_9[2]);
  not not_5 (not_5_out, out_9[7]);
  not not_6 (not_6_out, out_9[5]);
  not not_7 (not_7_out, out_9[4]);
  not not_8 (not_8_out, out_9[6]);
  not not_9 (not_9_out, out_9[3]);
  and and_34 (Zero, not_3_out, not_2_out, not_4_out, not_9_out, not_7_out, not_6_out, not_8_out, not_5_out);

  // Notes on the sheet:
  //   R
  //   L
  //   SUB Section OPCODE required
  //   MULT SECTION OPCODE
  //   1 = SUB ON 0 = SUB OFF
  //   1= MULT ON 0= MULT OFF
  //   ADD Section OPCODE required
  //   1 = ADD ON 0 = ADD OFF
  //   Multiplication has no signed overflow check. Beware when using it with signed integers.
  //   If there is an overflow, we can't tell the sign.
endmodule

module full_adder (
  input  in_1,
  input  in_2,
  input  in_3,
  output out_4,
  output out_5
);

  wire and_1_out, and_2_out, xor_1_out;

  xor xor_1 (xor_1_out, in_2, in_3);
  and and_1 (and_1_out, in_1, xor_1_out);
  or or_1 (out_5, and_1_out, and_2_out);
  and and_2 (and_2_out, in_2, in_3);
  xor xor_2 (out_4, in_1, xor_1_out);
endmodule

module half_adder (
  input  in_1,
  input  in_2,
  output out_3,
  output out_4
);

  xor xor_1 (out_3, in_1, in_2);
  and and_1 (out_4, in_1, in_2);
endmodule

module ALU2C (
  input  in_1,
  input  [7:0] in_2,
  output [7:0] out_3
);

  wire and_1_out, and_2_out, and_3_out, and_4_out, and_5_out, and_6_out, and_7_out, and_8_out, and_9_out,
       and_10_out, and_11_out, and_12_out, and_13_out, and_14_out, and_15_out, and_16_out,
       full_adder_1_out_5, full_adder_2_out_5, full_adder_3_out_5, full_adder_4_out_5, full_adder_5_out_5,
       full_adder_6_out_5, half_adder_1_out_4, not_1_out, not_2_out, not_3_out, not_4_out, not_5_out,
       not_6_out, not_7_out, not_8_out, not_9_out, not_10_out, not_11_out, not_12_out, not_13_out,
       not_14_out, not_15_out, not_16_out, or_1_out, or_2_out, or_3_out, or_4_out, or_5_out, or_6_out,
       or_7_out, or_8_out;

  not not_1 (not_1_out, in_1);
  not not_2 (not_2_out, in_2[0]);
  not not_3 (not_3_out, in_1);
  not not_4 (not_4_out, in_2[1]);
  not not_5 (not_5_out, in_1);
  not not_6 (not_6_out, in_2[2]);
  not not_7 (not_7_out, in_1);
  not not_8 (not_8_out, in_2[3]);
  not not_9 (not_9_out, in_1);
  not not_10 (not_10_out, in_2[4]);
  not not_11 (not_11_out, in_1);
  not not_12 (not_12_out, in_2[5]);
  not not_13 (not_13_out, in_1);
  not not_14 (not_14_out, in_2[6]);
  not not_15 (not_15_out, in_1);
  not not_16 (not_16_out, in_2[7]);
  and and_1 (and_1_out, not_1_out, in_2[0]);
  or or_1 (or_1_out, and_1_out, and_2_out);
  and and_2 (and_2_out, in_1, not_2_out);
  and and_3 (and_3_out, not_3_out, in_2[1]);
  or or_2 (or_2_out, and_3_out, and_4_out);
  and and_4 (and_4_out, in_1, not_4_out);
  and and_5 (and_5_out, not_5_out, in_2[2]);
  or or_3 (or_3_out, and_5_out, and_6_out);
  and and_6 (and_6_out, in_1, not_6_out);
  and and_7 (and_7_out, not_7_out, in_2[3]);
  or or_4 (or_4_out, and_7_out, and_8_out);
  and and_8 (and_8_out, in_1, not_8_out);
  and and_9 (and_9_out, not_9_out, in_2[4]);
  or or_5 (or_5_out, and_9_out, and_10_out);
  and and_10 (and_10_out, in_1, not_10_out);
  and and_11 (and_11_out, not_11_out, in_2[5]);
  or or_6 (or_6_out, and_11_out, and_12_out);
  and and_12 (and_12_out, in_1, not_12_out);
  and and_13 (and_13_out, not_13_out, in_2[6]);
  or or_7 (or_7_out, and_13_out, and_14_out);
  and and_14 (and_14_out, in_1, not_14_out);
  and and_15 (and_15_out, not_15_out, in_2[7]);
  or or_8 (or_8_out, and_15_out, and_16_out);
  and and_16 (and_16_out, in_1, not_16_out);
  half_adder half_adder_1 (.in_1(or_1_out), .in_2(in_1), .out_3(out_3[0]), .out_4(half_adder_1_out_4));
  full_adder full_adder_1 (
    .in_2(or_2_out), .in_3(1'b0), .out_4(out_3[1]), .in_1(half_adder_1_out_4), .out_5(full_adder_1_out_5));
  full_adder full_adder_2 (
    .in_2(or_3_out), .in_3(1'b0), .out_4(out_3[2]), .in_1(full_adder_1_out_5), .out_5(full_adder_2_out_5));
  full_adder full_adder_3 (
    .in_2(or_4_out), .in_3(1'b0), .out_4(out_3[3]), .in_1(full_adder_2_out_5), .out_5(full_adder_3_out_5));
  full_adder full_adder_4 (
    .in_2(or_5_out), .in_3(1'b0), .out_4(out_3[4]), .in_1(full_adder_3_out_5), .out_5(full_adder_4_out_5));
  full_adder full_adder_5 (
    .in_2(or_6_out), .in_3(1'b0), .out_4(out_3[5]), .in_1(full_adder_4_out_5), .out_5(full_adder_5_out_5));
  full_adder full_adder_6 (
    .in_2(or_7_out), .in_3(1'b0), .out_4(out_3[6]), .in_1(full_adder_5_out_5), .out_5(full_adder_6_out_5));
  full_adder full_adder_7 (.in_2(or_8_out), .in_3(1'b0), .out_4(out_3[7]), .in_1(full_adder_6_out_5));  // open: out_5
endmodule

module _16bitshift (
  input  [15:0] in_1,
  output [15:0] out_2
);


  assign out_2 = {in_1[14:0], 1'b0};
endmodule

module multhelper (
  input  [15:0] in_1,
  input  in_2,
  output [15:0] out_3
);

  and and_1 (out_3[0], in_1[0], in_2);
  and and_2 (out_3[1], in_1[1], in_2);
  and and_3 (out_3[2], in_1[2], in_2);
  and and_4 (out_3[3], in_1[3], in_2);
  and and_5 (out_3[4], in_1[4], in_2);
  and and_6 (out_3[5], in_1[5], in_2);
  and and_7 (out_3[6], in_1[6], in_2);
  and and_8 (out_3[7], in_1[7], in_2);
  and and_9 (out_3[8], in_1[8], in_2);
  and and_10 (out_3[9], in_1[9], in_2);
  and and_11 (out_3[10], in_1[10], in_2);
  and and_12 (out_3[11], in_1[11], in_2);
  and and_13 (out_3[12], in_1[12], in_2);
  and and_14 (out_3[13], in_1[13], in_2);
  and and_15 (out_3[14], in_1[14], in_2);
  and and_16 (out_3[15], in_1[15], in_2);
endmodule

module StatusRegister (
  input  CLK,
  input  R_W,
  input  ENABLE,
  input  [2:0] INPUT,
  output [2:0] out_5
);

  wire and_1_out, and_2_out, and_3_out, and_4_out, and_5_out, not_1_out, not_2_out, not_3_out, not_4_out,
       s_r_ff_1_q, s_r_ff_2_q, s_r_ff_3_q;

  and and_1 (and_1_out, CLK, ENABLE);
  and and_2 (and_2_out, CLK, R_W, ENABLE);
  and and_3 (and_3_out, INPUT[0], CLK, R_W);
  not not_1 (not_1_out, and_3_out);
  and and_4 (and_4_out, INPUT[1], CLK, R_W);
  not not_2 (not_2_out, and_4_out);
  and and_5 (and_5_out, INPUT[2], CLK, R_W);
  not not_3 (not_3_out, and_5_out);
  not not_4 (not_4_out, R_W);
  S_R_Flip_Flop #(.trigger("high")) s_r_ff_1 (
    .S(and_3_out), .clk(and_2_out), .R(not_1_out), .Q(s_r_ff_1_q));  // open: Qn, preset, reset, en
  S_R_Flip_Flop #(.trigger("high")) s_r_ff_2 (
    .S(and_4_out), .clk(and_2_out), .R(not_2_out), .Q(s_r_ff_2_q));  // open: Qn, preset, reset, en
  S_R_Flip_Flop #(.trigger("high")) s_r_ff_3 (
    .S(and_5_out), .clk(and_2_out), .R(not_3_out), .Q(s_r_ff_3_q));  // open: Qn, preset, reset, en
  and and_6 (out_5[0], s_r_ff_1_q, and_1_out, not_4_out);
  and and_7 (out_5[1], s_r_ff_2_q, and_1_out, not_4_out);
  and and_8 (out_5[2], s_r_ff_3_q, and_1_out, not_4_out);
endmodule

module _3_Combinator (
  input  in_1,
  input  [7:0] in_2,
  input  in_3,
  input  [7:0] in_4,
  input  in_5,
  input  [7:0] in_6,
  output [7:0] out_7
);

  wire and_1_out, and_2_out, and_3_out, and_4_out, and_5_out, and_6_out, and_7_out, and_8_out, and_9_out,
       and_10_out, and_11_out, and_12_out, and_13_out, and_14_out, and_15_out, and_16_out, and_17_out,
       and_18_out, and_19_out, and_20_out, and_21_out, and_22_out, and_23_out, and_24_out;

  and and_1 (and_1_out, in_2[0], in_1);
  and and_2 (and_2_out, in_2[1], in_1);
  and and_3 (and_3_out, in_2[2], in_1);
  and and_4 (and_4_out, in_2[3], in_1);
  and and_5 (and_5_out, in_2[4], in_1);
  and and_6 (and_6_out, in_2[5], in_1);
  and and_7 (and_7_out, in_2[6], in_1);
  and and_8 (and_8_out, in_2[7], in_1);
  and and_9 (and_9_out, in_4[0], in_3);
  and and_10 (and_10_out, in_4[1], in_3);
  and and_11 (and_11_out, in_4[2], in_3);
  and and_12 (and_12_out, in_4[3], in_3);
  and and_13 (and_13_out, in_4[4], in_3);
  and and_14 (and_14_out, in_4[5], in_3);
  and and_15 (and_15_out, in_4[6], in_3);
  and and_16 (and_16_out, in_4[7], in_3);
  and and_17 (and_17_out, in_6[0], in_5);
  and and_18 (and_18_out, in_6[1], in_5);
  and and_19 (and_19_out, in_6[2], in_5);
  and and_20 (and_20_out, in_6[3], in_5);
  and and_21 (and_21_out, in_6[4], in_5);
  and and_22 (and_22_out, in_6[5], in_5);
  and and_23 (and_23_out, in_6[6], in_5);
  and and_24 (and_24_out, in_6[7], in_5);
  or or_1 (out_7[0], and_1_out, and_9_out, and_17_out);
  or or_2 (out_7[1], and_2_out, and_10_out, and_18_out);
  or or_3 (out_7[2], and_3_out, and_11_out, and_19_out);
  or or_4 (out_7[3], and_4_out, and_12_out, and_20_out);
  or or_5 (out_7[4], and_5_out, and_13_out, and_21_out);
  or or_6 (out_7[5], and_6_out, and_14_out, and_22_out);
  or or_7 (out_7[6], and_7_out, and_15_out, and_23_out);
  or or_8 (out_7[7], and_8_out, and_16_out, and_24_out);
endmodule

module _4_combinator (
  input  in_1,
  input  [7:0] in_2,
  input  in_3,
  input  [7:0] in_4,
  input  in_5,
  input  [7:0] in_6,
  input  in_7,
  input  [7:0] in_8,
  output [7:0] out_9
);

  wire and_1_out, and_2_out, and_3_out, and_4_out, and_5_out, and_6_out, and_7_out, and_8_out, and_9_out,
       and_10_out, and_11_out, and_12_out, and_13_out, and_14_out, and_15_out, and_16_out, and_17_out,
       and_18_out, and_19_out, and_20_out, and_21_out, and_22_out, and_23_out, and_24_out, and_25_out,
       and_26_out, and_27_out, and_28_out, and_29_out, and_30_out, and_31_out, and_32_out;

  and and_1 (and_1_out, in_2[0], in_1);
  and and_2 (and_2_out, in_2[1], in_1);
  and and_3 (and_3_out, in_2[2], in_1);
  and and_4 (and_4_out, in_2[3], in_1);
  and and_5 (and_5_out, in_2[4], in_1);
  and and_6 (and_6_out, in_2[5], in_1);
  and and_7 (and_7_out, in_2[6], in_1);
  and and_8 (and_8_out, in_2[7], in_1);
  and and_9 (and_9_out, in_4[0], in_3);
  and and_10 (and_10_out, in_4[1], in_3);
  and and_11 (and_11_out, in_4[2], in_3);
  and and_12 (and_12_out, in_4[3], in_3);
  and and_13 (and_13_out, in_4[4], in_3);
  and and_14 (and_14_out, in_4[5], in_3);
  and and_15 (and_15_out, in_4[6], in_3);
  and and_16 (and_16_out, in_4[7], in_3);
  and and_17 (and_17_out, in_6[0], in_5);
  and and_18 (and_18_out, in_6[1], in_5);
  and and_19 (and_19_out, in_6[2], in_5);
  and and_20 (and_20_out, in_6[3], in_5);
  and and_21 (and_21_out, in_6[4], in_5);
  and and_22 (and_22_out, in_6[5], in_5);
  and and_23 (and_23_out, in_6[6], in_5);
  and and_24 (and_24_out, in_6[7], in_5);
  and and_25 (and_25_out, in_8[0], in_7);
  and and_26 (and_26_out, in_8[1], in_7);
  and and_27 (and_27_out, in_8[2], in_7);
  and and_28 (and_28_out, in_8[3], in_7);
  and and_29 (and_29_out, in_8[4], in_7);
  and and_30 (and_30_out, in_8[5], in_7);
  and and_31 (and_31_out, in_8[6], in_7);
  and and_32 (and_32_out, in_8[7], in_7);
  or or_1 (out_9[0], and_1_out, and_9_out, and_17_out, and_25_out);
  or or_2 (out_9[1], and_2_out, and_10_out, and_18_out, and_26_out);
  or or_3 (out_9[2], and_3_out, and_11_out, and_19_out, and_27_out);
  or or_4 (out_9[3], and_4_out, and_12_out, and_20_out, and_28_out);
  or or_5 (out_9[4], and_5_out, and_13_out, and_21_out, and_29_out);
  or or_6 (out_9[5], and_6_out, and_14_out, and_22_out, and_30_out);
  or or_7 (out_9[6], and_7_out, and_15_out, and_23_out, and_31_out);
  or or_8 (out_9[7], and_8_out, and_16_out, and_24_out, and_32_out);
endmodule

module _5_combinator (
  input  in_1,
  input  [7:0] in_2,
  input  in_3,
  input  [7:0] in_4,
  input  in_5,
  input  [7:0] in_6,
  input  in_7,
  input  [7:0] in_8,
  input  in_9,
  input  [7:0] in_10,
  output [7:0] out_11
);

  wire and_1_out, and_2_out, and_3_out, and_4_out, and_5_out, and_6_out, and_7_out, and_8_out, and_9_out,
       and_10_out, and_11_out, and_12_out, and_13_out, and_14_out, and_15_out, and_16_out, and_17_out,
       and_18_out, and_19_out, and_20_out, and_21_out, and_22_out, and_23_out, and_24_out, and_25_out,
       and_26_out, and_27_out, and_28_out, and_29_out, and_30_out, and_31_out, and_32_out, and_33_out,
       and_34_out, and_35_out, and_36_out, and_37_out, and_38_out, and_39_out, and_40_out;
  wire [7:0] or_1_out, or_9_out;

  and and_1 (and_1_out, in_2[0], in_1);
  and and_2 (and_2_out, in_2[1], in_1);
  and and_3 (and_3_out, in_2[2], in_1);
  and and_4 (and_4_out, in_2[3], in_1);
  and and_5 (and_5_out, in_2[4], in_1);
  and and_6 (and_6_out, in_2[5], in_1);
  and and_7 (and_7_out, in_2[6], in_1);
  and and_8 (and_8_out, in_2[7], in_1);
  and and_9 (and_9_out, in_4[0], in_3);
  and and_10 (and_10_out, in_4[1], in_3);
  and and_11 (and_11_out, in_4[2], in_3);
  and and_12 (and_12_out, in_4[3], in_3);
  and and_13 (and_13_out, in_4[4], in_3);
  and and_14 (and_14_out, in_4[5], in_3);
  and and_15 (and_15_out, in_4[6], in_3);
  and and_16 (and_16_out, in_4[7], in_3);
  and and_17 (and_17_out, in_6[0], in_5);
  and and_18 (and_18_out, in_6[1], in_5);
  and and_19 (and_19_out, in_6[2], in_5);
  and and_20 (and_20_out, in_6[3], in_5);
  and and_21 (and_21_out, in_6[4], in_5);
  and and_22 (and_22_out, in_6[5], in_5);
  and and_23 (and_23_out, in_6[6], in_5);
  and and_24 (and_24_out, in_6[7], in_5);
  and and_25 (and_25_out, in_8[0], in_7);
  and and_26 (and_26_out, in_8[1], in_7);
  and and_27 (and_27_out, in_8[2], in_7);
  and and_28 (and_28_out, in_8[3], in_7);
  and and_29 (and_29_out, in_8[4], in_7);
  and and_30 (and_30_out, in_8[5], in_7);
  and and_31 (and_31_out, in_8[6], in_7);
  and and_32 (and_32_out, in_8[7], in_7);
  and and_33 (and_33_out, in_10[0], in_9);
  and and_34 (and_34_out, in_10[1], in_9);
  and and_35 (and_35_out, in_10[2], in_9);
  and and_36 (and_36_out, in_10[3], in_9);
  and and_37 (and_37_out, in_10[4], in_9);
  and and_38 (and_38_out, in_10[5], in_9);
  and and_39 (and_39_out, in_10[6], in_9);
  and and_40 (and_40_out, in_10[7], in_9);
  or or_1 (or_1_out[0], and_1_out, and_9_out, and_17_out);
  or or_2 (or_1_out[1], and_2_out, and_10_out, and_18_out);
  or or_3 (or_1_out[2], and_3_out, and_11_out, and_19_out);
  or or_4 (or_1_out[3], and_4_out, and_12_out, and_20_out);
  or or_5 (or_1_out[4], and_5_out, and_13_out, and_21_out);
  or or_6 (or_1_out[5], and_6_out, and_14_out, and_22_out);
  or or_7 (or_1_out[6], and_7_out, and_15_out, and_23_out);
  or or_8 (or_1_out[7], and_8_out, and_16_out, and_24_out);
  or or_9 (or_9_out[0], and_25_out, and_33_out);
  or or_10 (or_9_out[1], and_26_out, and_34_out);
  or or_11 (or_9_out[2], and_27_out, and_35_out);
  or or_12 (or_9_out[3], and_28_out, and_36_out);
  or or_13 (or_9_out[4], and_29_out, and_37_out);
  or or_14 (or_9_out[5], and_30_out, and_38_out);
  or or_15 (or_9_out[6], and_31_out, and_39_out);
  or or_16 (or_9_out[7], and_32_out, and_40_out);
  assign out_11 = or_1_out | or_9_out;  // OR_Gate or_17, 8 bits wide
endmodule

module _2_Combinator (
  input  in_1,
  input  [7:0] in_2,
  input  in_3,
  input  [7:0] in_4,
  output [7:0] out_5
);

  wire and_1_out, and_2_out, and_3_out, and_4_out, and_5_out, and_6_out, and_7_out, and_8_out, and_9_out,
       and_10_out, and_11_out, and_12_out, and_13_out, and_14_out, and_15_out, and_16_out;

  and and_1 (and_1_out, in_2[0], in_1);
  and and_2 (and_2_out, in_2[1], in_1);
  and and_3 (and_3_out, in_2[2], in_1);
  and and_4 (and_4_out, in_2[3], in_1);
  and and_5 (and_5_out, in_2[4], in_1);
  and and_6 (and_6_out, in_2[5], in_1);
  and and_7 (and_7_out, in_2[6], in_1);
  and and_8 (and_8_out, in_2[7], in_1);
  and and_9 (and_9_out, in_4[0], in_3);
  and and_10 (and_10_out, in_4[1], in_3);
  and and_11 (and_11_out, in_4[2], in_3);
  and and_12 (and_12_out, in_4[3], in_3);
  and and_13 (and_13_out, in_4[4], in_3);
  and and_14 (and_14_out, in_4[5], in_3);
  and and_15 (and_15_out, in_4[6], in_3);
  and and_16 (and_16_out, in_4[7], in_3);
  or or_1 (out_5[0], and_1_out, and_9_out);
  or or_2 (out_5[1], and_2_out, and_10_out);
  or or_3 (out_5[2], and_3_out, and_11_out);
  or or_4 (out_5[3], and_4_out, and_12_out);
  or or_5 (out_5[4], and_5_out, and_13_out);
  or or_6 (out_5[5], and_6_out, and_14_out);
  or or_7 (out_5[6], and_7_out, and_15_out);
  or or_8 (out_5[7], and_8_out, and_16_out);
endmodule

module Incrementer (
  input  [7:0] in_1,
  output [7:0] out_2
);

  wire full_adder_1_out_5, full_adder_2_out_5, half_adder_1_out_4;

  half_adder half_adder_1 (.in_1(in_1[0]), .in_2(1'b1), .out_3(out_2[0]), .out_4(half_adder_1_out_4));
  full_adder full_adder_1 (
    .in_2(in_1[1]), .in_3(1'b0), .out_4(out_2[1]), .in_1(half_adder_1_out_4), .out_5(full_adder_1_out_5));
  full_adder full_adder_2 (
    .in_2(in_1[2]), .in_3(1'b0), .out_4(out_2[2]), .in_1(full_adder_1_out_5), .out_5(full_adder_2_out_5));
  full_adder full_adder_3 (.in_2(in_1[3]), .in_3(1'b0), .out_4(out_2[3]), .in_1(full_adder_2_out_5));  // open: out_5

  assign out_2[7:4] = 4'b0000;
endmodule

module PCregister (
  input  CLK,
  input  R_W,
  input  ENABLE,
  input  [7:0] in_4,
  input  [2:0] in_5,
  input  in_6,
  output [7:0] out_7
);

  wire and_1_out, and_2_out, and_3_out, and_4_out, and_5_out, and_6_out, and_7_out, multiplexer_1_out,
       multiplexer_2_out, multiplexer_3_out, not_1_out, not_2_out, not_3_out, not_4_out, not_5_out,
       not_6_out, s_r_ff_1_q, s_r_ff_2_q, s_r_ff_3_q, s_r_ff_4_q;

  Multiplexer #(.disabled(0), .enable("false")) multiplexer_1 (
    .in0(in_4[0]), .in1(in_5[0]), .out(multiplexer_1_out), .sel(in_6));
  Multiplexer #(.disabled(0), .enable("false")) multiplexer_2 (
    .in0(in_4[1]), .in1(in_5[1]), .out(multiplexer_2_out), .sel(in_6));
  Multiplexer #(.disabled(0), .enable("false")) multiplexer_3 (
    .in0(in_4[2]), .in1(in_5[2]), .out(multiplexer_3_out), .sel(in_6));
  and and_1 (and_1_out, CLK, ENABLE);
  and and_2 (and_2_out, and_3_out, not_1_out);
  not not_1 (not_1_out, in_6);
  and and_3 (and_3_out, CLK, R_W, ENABLE);
  and and_4 (and_4_out, multiplexer_1_out, CLK, R_W);
  and and_5 (and_5_out, multiplexer_2_out, CLK, R_W);
  and and_6 (and_6_out, multiplexer_3_out, CLK, R_W);
  and and_7 (and_7_out, in_4[3], CLK, R_W);
  not not_2 (not_2_out, R_W);
  S_R_Flip_Flop #(.trigger("high")) s_r_ff_1 (
    .S(and_4_out), .clk(and_3_out), .R(not_3_out), .Q(s_r_ff_1_q));  // open: Qn, preset, reset, en
  not not_3 (not_3_out, and_4_out);
  S_R_Flip_Flop #(.trigger("high")) s_r_ff_2 (
    .S(and_5_out), .clk(and_3_out), .R(not_4_out), .Q(s_r_ff_2_q));  // open: Qn, preset, reset, en
  not not_4 (not_4_out, and_5_out);
  S_R_Flip_Flop #(.trigger("high")) s_r_ff_3 (
    .S(and_6_out), .clk(and_3_out), .R(not_5_out), .Q(s_r_ff_3_q));  // open: Qn, preset, reset, en
  not not_5 (not_5_out, and_6_out);
  S_R_Flip_Flop #(.trigger("high")) s_r_ff_4 (
    .S(and_7_out), .clk(and_2_out), .R(not_6_out), .Q(s_r_ff_4_q));  // open: Qn, preset, reset, en
  not not_6 (not_6_out, and_7_out);
  and and_8 (out_7[0], s_r_ff_1_q, and_1_out, not_2_out);
  and and_9 (out_7[1], s_r_ff_2_q, and_1_out, not_2_out);
  and and_10 (out_7[2], s_r_ff_3_q, and_1_out, not_2_out);
  and and_11 (out_7[3], s_r_ff_4_q, and_1_out, not_2_out);

  assign out_7[7:4] = 4'b0000;

  // Notes on the sheet:
  //   INPUT
endmodule

module register (
  input  CLK,
  input  R_W,
  input  ENABLE,
  input  [7:0] INPUT,
  output [7:0] out_5
);

  wire and_1_out, and_2_out, and_3_out, and_4_out, and_5_out, and_6_out, and_7_out, and_8_out, and_9_out,
       and_10_out, not_1_out, not_2_out, not_3_out, not_4_out, not_5_out, not_6_out, not_7_out, not_8_out,
       not_9_out, s_r_ff_1_q, s_r_ff_2_q, s_r_ff_3_q, s_r_ff_4_q, s_r_ff_5_q, s_r_ff_6_q, s_r_ff_7_q,
       s_r_ff_8_q;

  and and_1 (and_1_out, CLK, ENABLE);
  and and_2 (and_2_out, CLK, R_W, ENABLE);
  and and_3 (and_3_out, INPUT[0], CLK, R_W);
  not not_1 (not_1_out, and_3_out);
  and and_4 (and_4_out, INPUT[1], CLK, R_W);
  not not_2 (not_2_out, and_4_out);
  and and_5 (and_5_out, INPUT[2], CLK, R_W);
  not not_3 (not_3_out, and_5_out);
  and and_6 (and_6_out, INPUT[3], CLK, R_W);
  not not_4 (not_4_out, and_6_out);
  and and_7 (and_7_out, INPUT[4], CLK, R_W);
  not not_5 (not_5_out, and_7_out);
  and and_8 (and_8_out, INPUT[5], CLK, R_W);
  not not_6 (not_6_out, and_8_out);
  and and_9 (and_9_out, INPUT[6], CLK, R_W);
  not not_7 (not_7_out, and_9_out);
  and and_10 (and_10_out, INPUT[7], CLK, R_W);
  not not_8 (not_8_out, and_10_out);
  not not_9 (not_9_out, R_W);
  S_R_Flip_Flop #(.trigger("high")) s_r_ff_1 (
    .S(and_3_out), .clk(and_2_out), .R(not_1_out), .Q(s_r_ff_1_q));  // open: Qn, preset, reset, en
  S_R_Flip_Flop #(.trigger("high")) s_r_ff_2 (
    .S(and_4_out), .clk(and_2_out), .R(not_2_out), .Q(s_r_ff_2_q));  // open: Qn, preset, reset, en
  S_R_Flip_Flop #(.trigger("high")) s_r_ff_3 (
    .S(and_5_out), .clk(and_2_out), .R(not_3_out), .Q(s_r_ff_3_q));  // open: Qn, preset, reset, en
  S_R_Flip_Flop #(.trigger("high")) s_r_ff_4 (
    .S(and_6_out), .clk(and_2_out), .R(not_4_out), .Q(s_r_ff_4_q));  // open: Qn, preset, reset, en
  S_R_Flip_Flop #(.trigger("high")) s_r_ff_5 (
    .S(and_7_out), .clk(and_2_out), .R(not_5_out), .Q(s_r_ff_5_q));  // open: Qn, preset, reset, en
  S_R_Flip_Flop #(.trigger("high")) s_r_ff_6 (
    .S(and_8_out), .clk(and_2_out), .R(not_6_out), .Q(s_r_ff_6_q));  // open: Qn, preset, reset, en
  S_R_Flip_Flop #(.trigger("high")) s_r_ff_7 (
    .S(and_9_out), .clk(and_2_out), .R(not_7_out), .Q(s_r_ff_7_q));  // open: Qn, preset, reset, en
  S_R_Flip_Flop #(.trigger("high")) s_r_ff_8 (
    .S(and_10_out), .clk(and_2_out), .R(not_8_out), .Q(s_r_ff_8_q));  // open: Qn, preset, reset, en
  and and_11 (out_5[0], s_r_ff_1_q, and_1_out, not_9_out);
  and and_12 (out_5[1], s_r_ff_2_q, and_1_out, not_9_out);
  and and_13 (out_5[2], s_r_ff_3_q, and_1_out, not_9_out);
  and and_14 (out_5[3], s_r_ff_4_q, and_1_out, not_9_out);
  and and_15 (out_5[4], s_r_ff_5_q, and_1_out, not_9_out);
  and and_16 (out_5[5], s_r_ff_6_q, and_1_out, not_9_out);
  and and_17 (out_5[6], s_r_ff_7_q, and_1_out, not_9_out);
  and and_18 (out_5[7], s_r_ff_8_q, and_1_out, not_9_out);
endmodule

module DR (
  input  CLK,
  input  R_W,
  input  ENABLE,
  input  [7:0] INPUT_1,
  input  in_5,
  input  [7:0] INPUT_2,
  output [7:0] OUTPUT1,
  output [7:0] OUTPUT2
);

  wire and_1_out, and_2_out, and_3_out, and_4_out, and_5_out, and_6_out, and_7_out, and_8_out, and_9_out,
       and_10_out, and_11_out, and_12_out, and_13_out, and_14_out, and_15_out, and_16_out, and_17_out,
       and_18_out, and_19_out, and_20_out, and_21_out, and_22_out, and_23_out, and_24_out, and_25_out,
       and_26_out, and_27_out, and_28_out, and_29_out, and_30_out, and_31_out, and_32_out, and_33_out,
       and_34_out, not_1_out, not_2_out, not_3_out, not_4_out, not_5_out, not_6_out, not_7_out, not_8_out,
       not_9_out, not_10_out, not_11_out, or_1_out, or_2_out, or_3_out, or_4_out, or_5_out, or_6_out,
       or_7_out, or_8_out, s_r_ff_1_q, s_r_ff_2_q, s_r_ff_3_q, s_r_ff_4_q, s_r_ff_5_q, s_r_ff_6_q,
       s_r_ff_7_q, s_r_ff_8_q;

  and and_1 (and_1_out, INPUT_1[0], not_1_out);
  and and_2 (and_2_out, INPUT_1[1], not_1_out);
  and and_3 (and_3_out, INPUT_1[2], not_1_out);
  and and_4 (and_4_out, INPUT_1[3], not_1_out);
  and and_5 (and_5_out, INPUT_1[4], not_1_out);
  and and_6 (and_6_out, INPUT_1[5], not_1_out);
  and and_7 (and_7_out, INPUT_1[6], not_1_out);
  and and_8 (and_8_out, INPUT_1[7], not_1_out);
  not not_1 (not_1_out, in_5);
  and and_9 (and_9_out, in_5, INPUT_2[0]);
  and and_10 (and_10_out, in_5, INPUT_2[1]);
  and and_11 (and_11_out, in_5, INPUT_2[2]);
  and and_12 (and_12_out, in_5, INPUT_2[3]);
  and and_13 (and_13_out, in_5, INPUT_2[4]);
  and and_14 (and_14_out, in_5, INPUT_2[5]);
  and and_15 (and_15_out, in_5, INPUT_2[6]);
  and and_16 (and_16_out, in_5, INPUT_2[7]);
  or or_1 (or_1_out, and_1_out, and_9_out);
  or or_2 (or_2_out, and_2_out, and_10_out);
  or or_3 (or_3_out, and_3_out, and_11_out);
  or or_4 (or_4_out, and_4_out, and_12_out);
  or or_5 (or_5_out, and_5_out, and_13_out);
  or or_6 (or_6_out, and_6_out, and_14_out);
  or or_7 (or_7_out, and_7_out, and_15_out);
  or or_8 (or_8_out, and_8_out, and_16_out);
  and and_17 (and_17_out, CLK, ENABLE);
  and and_18 (and_18_out, CLK, R_W, ENABLE);
  and and_19 (and_19_out, or_1_out, CLK, R_W);
  not not_2 (not_2_out, and_19_out);
  and and_20 (and_20_out, or_2_out, CLK, R_W);
  not not_3 (not_3_out, and_20_out);
  and and_21 (and_21_out, or_3_out, CLK, R_W);
  not not_4 (not_4_out, and_21_out);
  and and_22 (and_22_out, or_4_out, CLK, R_W);
  not not_5 (not_5_out, and_22_out);
  and and_23 (and_23_out, or_5_out, CLK, R_W);
  not not_6 (not_6_out, and_23_out);
  and and_24 (and_24_out, or_6_out, CLK, R_W);
  not not_7 (not_7_out, and_24_out);
  and and_25 (and_25_out, or_7_out, CLK, R_W);
  not not_8 (not_8_out, and_25_out);
  and and_26 (and_26_out, or_8_out, CLK, R_W);
  not not_9 (not_9_out, and_26_out);
  not not_10 (not_10_out, R_W);
  S_R_Flip_Flop #(.trigger("high")) s_r_ff_1 (
    .S(and_19_out), .clk(and_18_out), .R(not_2_out), .Q(s_r_ff_1_q));  // open: Qn, preset, reset, en
  and and_27 (and_27_out, s_r_ff_1_q, and_17_out, not_10_out);
  S_R_Flip_Flop #(.trigger("high")) s_r_ff_2 (
    .S(and_20_out), .clk(and_18_out), .R(not_3_out), .Q(s_r_ff_2_q));  // open: Qn, preset, reset, en
  and and_28 (and_28_out, s_r_ff_2_q, and_17_out, not_10_out);
  S_R_Flip_Flop #(.trigger("high")) s_r_ff_3 (
    .S(and_21_out), .clk(and_18_out), .R(not_4_out), .Q(s_r_ff_3_q));  // open: Qn, preset, reset, en
  and and_29 (and_29_out, s_r_ff_3_q, and_17_out, not_10_out);
  S_R_Flip_Flop #(.trigger("high")) s_r_ff_4 (
    .S(and_22_out), .clk(and_18_out), .R(not_5_out), .Q(s_r_ff_4_q));  // open: Qn, preset, reset, en
  and and_30 (and_30_out, s_r_ff_4_q, and_17_out, not_10_out);
  S_R_Flip_Flop #(.trigger("high")) s_r_ff_5 (
    .S(and_23_out), .clk(and_18_out), .R(not_6_out), .Q(s_r_ff_5_q));  // open: Qn, preset, reset, en
  and and_31 (and_31_out, s_r_ff_5_q, and_17_out, not_10_out);
  S_R_Flip_Flop #(.trigger("high")) s_r_ff_6 (
    .S(and_24_out), .clk(and_18_out), .R(not_7_out), .Q(s_r_ff_6_q));  // open: Qn, preset, reset, en
  and and_32 (and_32_out, s_r_ff_6_q, and_17_out, not_10_out);
  S_R_Flip_Flop #(.trigger("high")) s_r_ff_7 (
    .S(and_25_out), .clk(and_18_out), .R(not_8_out), .Q(s_r_ff_7_q));  // open: Qn, preset, reset, en
  and and_33 (and_33_out, s_r_ff_7_q, and_17_out, not_10_out);
  S_R_Flip_Flop #(.trigger("high")) s_r_ff_8 (
    .S(and_26_out), .clk(and_18_out), .R(not_9_out), .Q(s_r_ff_8_q));  // open: Qn, preset, reset, en
  and and_34 (and_34_out, s_r_ff_8_q, and_17_out, not_10_out);
  not not_11 (not_11_out, in_5);
  and and_35 (OUTPUT1[0], and_27_out, not_11_out);
  and and_36 (OUTPUT1[1], and_28_out, not_11_out);
  and and_37 (OUTPUT1[2], and_29_out, not_11_out);
  and and_38 (OUTPUT1[3], and_30_out, not_11_out);
  and and_39 (OUTPUT1[4], and_31_out, not_11_out);
  and and_40 (OUTPUT1[5], and_32_out, not_11_out);
  and and_41 (OUTPUT1[6], and_33_out, not_11_out);
  and and_42 (OUTPUT1[7], and_34_out, not_11_out);
  and and_43 (OUTPUT2[0], in_5, and_27_out);
  and and_44 (OUTPUT2[1], in_5, and_28_out);
  and and_45 (OUTPUT2[2], in_5, and_29_out);
  and and_46 (OUTPUT2[3], in_5, and_30_out);
  and and_47 (OUTPUT2[4], in_5, and_31_out);
  and and_48 (OUTPUT2[5], in_5, and_32_out);
  and and_49 (OUTPUT2[6], in_5, and_33_out);
  and and_50 (OUTPUT2[7], in_5, and_34_out);
endmodule

module MEMORY_CONTROL_UNIT (
  input  CLOCK,
  input  ENABLE,
  input  [7:0] INPUT,
  input  bit2,
  input  bit1,
  input  bit0,
  output [7:0] AR_INPUT,
  output AR_CLK,
  output AR_R_W,
  output AR_ENABLE,
  output RAM_CLK,
  output RAM_R_W,
  output [7:0] DR_INPUT,
  output DR_CLK,
  output DR_R_W,
  output DR_ENABLE,
  output DR_DIRECTION,
  output DONE_FLAG
);

  wire and_1_out, and_2_out, and_3_out, and_4_out, and_5_out, and_6_out, and_7_out, and_8_out, and_9_out,
       and_10_out, L_2_out, L_3_out, L_4_out, L_5_out, L_6_out, L_7_out, L_8_out, L_9_out, L_out, LOAD_out,
       not_1_out, not_2_out, not_3_out, not_4_out, not_5_out, not_6_out, not_7_out, not_8_out, not_9_out,
       not_10_out, not_11_out, not_12_out, not_13_out, not_14_out, or_1_out, or_2_out, S_2_out, S_3_out,
       S_4_out, S_5_out, S_6_out, S_out, s_r_ff_1_q, s_r_ff_2_q, STORE_out, TICK0_out, TICK1_out, TICK2_out,
       TICK3_out;
  wire [7:0] n8bitgate_1_out_4, n8bitgate_2_out_4, n8bitgate_3_out_4;

  or or_1 (or_1_out, 1'b0, TICK2_out, 1'b0, TICK0_out);
  not not_1 (not_1_out, or_1_out);
  not not_2 (not_2_out, or_2_out);
  or or_2 (or_2_out, 1'b0, TICK2_out, TICK1_out, 1'b0);
  S_R_Flip_Flop s_r_ff_1 (.S(or_1_out), .clk(CLOCK), .R(not_1_out), .Q(s_r_ff_1_q));  // open: Qn, preset, reset, en
  S_R_Flip_Flop s_r_ff_2 (.S(or_2_out), .clk(CLOCK), .R(not_2_out), .Q(s_r_ff_2_q));  // open: Qn, preset, reset, en
  not not_3 (not_3_out, s_r_ff_2_q);
  not not_4 (not_4_out, s_r_ff_1_q);
  and TICK0 (TICK0_out, not_3_out, not_4_out);
  not not_5 (not_5_out, s_r_ff_2_q);
  and TICK1 (TICK1_out, not_5_out, s_r_ff_1_q);
  not not_6 (not_6_out, s_r_ff_1_q);
  and TICK2 (TICK2_out, s_r_ff_2_q, not_6_out);
  and TICK3 (TICK3_out, s_r_ff_2_q, s_r_ff_1_q);
  not not_7 (not_7_out, bit0);
  not not_8 (not_8_out, bit2);
  not not_9 (not_9_out, bit1);
  and LOAD (LOAD_out, not_7_out, not_9_out, not_8_out, ENABLE);
  and and_1 (and_1_out, ENABLE, TICK0_out);
  and and_2 (and_2_out, ENABLE, TICK1_out);
  and and_3 (and_3_out, ENABLE, TICK2_out);
  and and_4 (and_4_out, ENABLE, TICK3_out);
  not not_10 (not_10_out, bit1);
  not not_11 (not_11_out, bit0);
  and STORE (STORE_out, not_11_out, not_10_out, bit2, ENABLE);
  not not_12 (not_12_out, bit2);
  not not_13 (not_13_out, bit0);
  // AND_Gate BEQ has open pins: in0=not_13_out, in1=bit1, in2=not_12_out, in3=ENABLE, out=open
  not not_14 (not_14_out, bit0);
  // AND_Gate BNQ has open pins: in0=not_14_out, in1=bit1, in2=bit2, in3=ENABLE, out=open
  _8bitGATE u_8bitgate_1 (.INSTRUCTION(LOAD_out), .CLOCK(and_1_out), .INPUT(INPUT), .out_4(n8bitgate_1_out_4));
  and and_5 (and_5_out, LOAD_out, and_1_out);
  and and_6 (and_6_out, LOAD_out, and_2_out);
  and and_7 (and_7_out, LOAD_out, and_3_out);
  _8bitGATE u_8bitgate_2 (.INSTRUCTION(STORE_out), .CLOCK(and_1_out), .INPUT(INPUT), .out_4(n8bitgate_2_out_4));
  and and_8 (and_8_out, STORE_out, and_1_out);
  _8bitGATE u_8bitgate_3 (.INSTRUCTION(STORE_out), .CLOCK(and_2_out), .INPUT(INPUT), .out_4(n8bitgate_3_out_4));
  and and_9 (and_9_out, STORE_out, and_2_out);
  and and_10 (and_10_out, and_3_out, STORE_out);
  or L (L_out, and_5_out, and_6_out);
  or S (S_out, and_8_out, 1'b0, and_10_out);
  or L_2 (L_2_out, and_5_out, 1'b0);
  or S_2 (S_2_out, and_8_out, 1'b0, 1'b0);
  or L_3 (L_3_out, and_5_out, and_6_out);
  or S_3 (S_3_out, and_8_out, 1'b0, and_10_out);
  or L_4 (L_4_out, 1'b0, and_6_out);
  or L_5 (L_5_out, 1'b0, 1'b0);
  _2_Combinator u_2_combinator_1 (
    .in_2({8{1'b0}}), .in_4(n8bitgate_3_out_4), .out_5(DR_INPUT), .in_1(1'b0), .in_3(and_9_out));
  or L_6 (L_6_out, 1'b0, and_6_out, and_7_out);
  or S_4 (S_4_out, 1'b0, and_9_out, and_10_out);
  or L_7 (L_7_out, 1'b0, and_6_out, 1'b0);
  or S_5 (S_5_out, 1'b0, and_9_out, 1'b0);
  or L_8 (L_8_out, 1'b0, and_6_out, and_7_out);
  or S_6 (S_6_out, 1'b0, and_9_out, and_10_out);
  or L_9 (L_9_out, 1'b0, and_6_out, and_7_out);
  _2_Combinator u_2_combinator_2 (
    .in_2(n8bitgate_1_out_4), .in_4(n8bitgate_2_out_4), .out_5(AR_INPUT), .in_1(and_5_out), .in_3(and_8_out));
  or or_3 (AR_CLK, L_out, S_out);
  or or_4 (AR_R_W, L_2_out, S_2_out);
  or or_5 (AR_ENABLE, L_3_out, S_3_out);
  or or_6 (RAM_CLK, L_4_out, and_10_out);
  or or_7 (RAM_R_W, L_5_out, and_10_out);
  or or_8 (DR_CLK, L_6_out, S_4_out);
  or or_9 (DR_R_W, L_7_out, S_5_out);
  or or_10 (DR_ENABLE, L_8_out, S_6_out);
  or or_11 (DR_DIRECTION, L_9_out, 1'b0);
  or or_12 (DONE_FLAG, and_4_out, and_4_out);
endmodule

module _8bitGATE (
  input  INSTRUCTION,
  input  CLOCK,
  input  [7:0] INPUT,
  output [7:0] out_4
);

  and and_1 (out_4[0], INSTRUCTION, CLOCK, INPUT[0]);
  and and_2 (out_4[1], INSTRUCTION, CLOCK, INPUT[1]);
  and and_3 (out_4[2], INSTRUCTION, CLOCK, INPUT[2]);
  and and_4 (out_4[3], INSTRUCTION, CLOCK, INPUT[3]);
  and and_5 (out_4[4], INSTRUCTION, CLOCK, INPUT[4]);
  and and_6 (out_4[5], INSTRUCTION, CLOCK, INPUT[5]);
  and and_7 (out_4[6], INSTRUCTION, CLOCK, INPUT[6]);
  and and_8 (out_4[7], INSTRUCTION, CLOCK, INPUT[7]);
endmodule
module CU (
  input  in_1,
  input  [7:0] OP_CODE,
  input  STATUS_ZERO_FLAG,
  output D0_EN,
  output D0_RW,
  output D1_EN,
  output D1_RW,
  output L_EN,
  output L_RW,
  output R_EN,
  output R_RW,
  output A_EN,
  output A_RW,
  output STATUS_EN,
  output STATUS_RW,
  output MBR_EN,
  output MBR_RW,
  output MAR_EN,
  output MAR_RW
);

  wire _1_2_out, _1_out, _2_2_out, _2_out, _3_2_out, _3_out, _4_2_out, _4_out, _5_2_out, _5_out, _6_2_out,
       _6_out, _7_2_out, _7_out, _8_2_out, _8_out, _9_2_out, _9_out, _10_2_out, _10_out, _11_2_out, _11_out,
       _12_2_out, _12_out, and_1_out, and_2_out, and_3_out, and_4_out, and_5_out, and_6_out, and_7_out,
       and_8_out, and_9_out, and_10_out, and_11_out, and_12_out, and_13_out, and_14_out, and_15_out,
       and_16_out, and_17_out, and_18_out, and_19_out, and_20_out, and_21_out, and_22_out, and_23_out,
       and_24_out, and_25_out, and_26_out, and_27_out, and_28_out, and_29_out, and_30_out, and_31_out,
       and_32_out, and_33_out, and_34_out, and_35_out, and_36_out, and_37_out, and_38_out, and_39_out,
       and_40_out, and_41_out, and_42_out, and_43_out, and_44_out, and_45_out, and_46_out, and_47_out,
       and_48_out, and_49_out, and_50_out, and_51_out, and_52_out, and_53_out, and_54_out, and_55_out,
       and_56_out, and_57_out, and_58_out, and_59_out, and_60_out, and_61_out, and_62_out, and_63_out,
       and_64_out, and_65_out, and_66_out, and_67_out, and_68_out, and_69_out, and_70_out, and_71_out,
       and_72_out, and_73_out, and_74_out, and_75_out, and_76_out, and_77_out, and_78_out, and_79_out,
       and_80_out, and_81_out, and_82_out, and_83_out, and_84_out, and_85_out, and_86_out, and_87_out,
       and_88_out, and_89_out, and_90_out, and_91_out, and_92_out, and_93_out, and_94_out, and_95_out,
       and_96_out, and_97_out, and_98_out, and_99_out, and_100_out, and_101_out, and_102_out, and_103_out,
       and_104_out, and_105_out, and_106_out, and_107_out, and_108_out, and_109_out, and_110_out,
       and_111_out, and_112_out, and_113_out, and_114_out, and_115_out, and_116_out, and_117_out,
       and_118_out, and_119_out, and_120_out, and_121_out, and_122_out, and_123_out, and_124_out,
       and_125_out, and_126_out, and_127_out, and_128_out, and_129_out, and_130_out, and_131_out,
       and_132_out, and_133_out, and_134_out, and_135_out, and_136_out, and_137_out, and_138_out,
       and_139_out, and_140_out, and_141_out, and_142_out, and_143_out, and_144_out, and_145_out,
       and_146_out, and_147_out, and_148_out, and_149_out, and_150_out, and_151_out, and_152_out,
       and_153_out, and_154_out, and_155_out, and_156_out, and_157_out, and_158_out, and_159_out,
       and_160_out, and_161_out, and_162_out, and_163_out, and_164_out, and_165_out, and_166_out,
       and_167_out, and_168_out, and_169_out, and_170_out, and_171_out, and_172_out, and_173_out,
       and_174_out, and_175_out, and_176_out, and_177_out, and_178_out, clock_1_out, d_ff_1_q, d_ff_2_q,
       d_ff_3_q, d_ff_4_q, not_1_out, not_2_out, not_3_out, not_4_out, not_5_out, not_6_out, not_7_out,
       not_8_out, not_9_out, not_10_out, not_11_out, not_12_out, not_13_out, not_14_out, not_15_out,
       not_16_out, not_17_out, not_18_out, not_19_out, not_20_out, not_21_out, not_22_out, not_23_out,
       not_24_out, not_25_out, not_26_out, not_27_out, not_28_out, not_29_out, not_30_out, not_31_out,
       not_32_out, not_33_out, not_34_out, not_35_out, not_36_out, not_37_out, not_38_out, not_39_out,
       not_40_out, not_41_out, not_42_out, not_43_out, not_44_out, not_45_out, not_46_out, not_47_out,
       not_48_out, not_49_out, not_50_out, not_51_out, not_52_out, not_53_out, not_54_out, not_55_out,
       not_56_out, not_57_out, not_58_out, not_59_out, not_60_out, not_61_out, not_62_out, not_64_out,
       not_65_out, not_66_out, not_67_out, not_68_out, not_69_out, not_70_out, or_1_out, or_2_out, or_3_out,
       or_4_out, or_5_out, or_6_out, or_7_out, or_8_out, or_9_out, or_10_out, or_11_out, or_12_out,
       or_13_out, or_14_out, or_15_out, or_16_out;

  or or_1 (or_1_out, _11_out, _10_out, _9_out, _8_out);
  or or_2 (or_2_out, _7_out, _6_out, _5_out, _4_out);
  or or_3 (or_3_out, _11_out, _10_out, _7_out, _6_out, _2_out, _3_out);
  Clock clock_1 (.out(clock_1_out));
  or or_4 (or_4_out, _11_out, _9_out, _7_out, _5_out, _1_out, _3_out);
  D_Flip_Flop d_ff_1 (.clk(clock_1_out), .D(or_1_out), .Q(d_ff_1_q));  // open: Qn, preset, en, reset
  D_Flip_Flop d_ff_2 (.clk(clock_1_out), .D(or_2_out), .Q(d_ff_2_q));  // open: Qn, preset, en, reset
  D_Flip_Flop d_ff_3 (.clk(clock_1_out), .D(or_3_out), .Q(d_ff_3_q));  // open: Qn, preset, en, reset
  D_Flip_Flop d_ff_4 (.clk(clock_1_out), .D(or_4_out), .Q(d_ff_4_q));  // open: Qn, preset, en, reset
  not not_1 (not_1_out, d_ff_3_q);
  not not_2 (not_2_out, d_ff_2_q);
  not not_3 (not_3_out, d_ff_1_q);
  not not_4 (not_4_out, d_ff_4_q);
  and _1 (_1_out, not_3_out, not_2_out, not_1_out, not_4_out);
  not not_5 (not_5_out, d_ff_1_q);
  not not_6 (not_6_out, d_ff_1_q);
  not not_7 (not_7_out, d_ff_2_q);
  not not_8 (not_8_out, d_ff_3_q);
  and _2 (_2_out, not_5_out, not_7_out, not_8_out, d_ff_4_q);
  not not_9 (not_9_out, d_ff_4_q);
  not not_10 (not_10_out, d_ff_2_q);
  not not_11 (not_11_out, d_ff_2_q);
  not not_12 (not_12_out, d_ff_1_q);
  and _4 (_4_out, not_12_out, not_11_out, d_ff_3_q, d_ff_4_q);
  and _3 (_3_out, not_6_out, not_10_out, d_ff_3_q, not_9_out);
  not not_13 (not_13_out, d_ff_1_q);
  not not_14 (not_14_out, d_ff_4_q);
  not not_15 (not_15_out, d_ff_3_q);
  and _5 (_5_out, not_13_out, d_ff_2_q, not_15_out, not_14_out);
  not not_16 (not_16_out, d_ff_3_q);
  not not_17 (not_17_out, d_ff_1_q);
  not not_18 (not_18_out, d_ff_1_q);
  and _6 (_6_out, not_18_out, d_ff_2_q, not_16_out, d_ff_4_q);
  not not_19 (not_19_out, d_ff_4_q);
  not not_20 (not_20_out, d_ff_1_q);
  and _7 (_7_out, not_17_out, d_ff_2_q, d_ff_3_q, not_19_out);
  and _8 (_8_out, not_20_out, d_ff_2_q, d_ff_3_q, d_ff_4_q);
  not not_21 (not_21_out, d_ff_3_q);
  not not_22 (not_22_out, d_ff_4_q);
  not not_23 (not_23_out, d_ff_2_q);
  and _9 (_9_out, d_ff_1_q, not_23_out, not_21_out, not_22_out);
  buf and_1 (and_1_out, _1_2_out);  // AND_Gate
  not not_24 (not_24_out, d_ff_2_q);
  not not_25 (not_25_out, d_ff_3_q);
  and _10 (_10_out, d_ff_1_q, not_24_out, not_25_out, d_ff_4_q);
  buf and_2 (and_2_out, _1_2_out);  // AND_Gate
  not not_26 (not_26_out, d_ff_2_q);
  not not_27 (not_27_out, d_ff_2_q);
  not not_28 (not_28_out, d_ff_4_q);
  and _12 (_12_out, d_ff_1_q, not_26_out, d_ff_3_q, d_ff_4_q);
  and _11 (_11_out, d_ff_1_q, not_27_out, d_ff_3_q, not_28_out);
  buf and_3 (and_3_out, _1_2_out);  // AND_Gate
  and _1_2 (_1_2_out, in_1, _1_out);
  and _2_2 (_2_2_out, in_1, _2_out);
  and _3_2 (_3_2_out, in_1, _3_out);
  and _4_2 (_4_2_out, in_1, _4_out);
  and _5_2 (_5_2_out, in_1, _5_out);
  and _6_2 (_6_2_out, in_1, _6_out);
  and _7_2 (_7_2_out, in_1, _7_out);
  and _8_2 (_8_2_out, in_1, _8_out);
  and _9_2 (_9_2_out, in_1, _9_out);
  and _10_2 (_10_2_out, in_1, _10_out);
  and _11_2 (_11_2_out, in_1, _11_out);
  and _12_2 (_12_2_out, in_1, _12_out);
  buf and_4 (and_4_out, _1_2_out);  // AND_Gate
  or or_5 (or_5_out, and_2_out, and_12_out);
  buf and_5 (and_5_out, _1_2_out);  // AND_Gate
  buf and_6 (and_6_out, _2_2_out);  // AND_Gate
  or or_6 (or_6_out, and_3_out, and_8_out);
  buf and_7 (and_7_out, _2_2_out);  // AND_Gate
  buf and_8 (and_8_out, _2_2_out);  // AND_Gate
  or or_7 (or_7_out, and_5_out, and_6_out);
  buf and_9 (and_9_out, _2_2_out);  // AND_Gate
  buf and_10 (and_10_out, _2_2_out);  // AND_Gate
  buf and_11 (and_11_out, _2_2_out);  // AND_Gate
  buf and_12 (and_12_out, _2_2_out);  // AND_Gate
  buf and_13 (and_13_out, _3_2_out);  // AND_Gate
  buf and_14 (and_14_out, _4_2_out);  // AND_Gate
  or or_8 (or_8_out, and_11_out, and_13_out, and_14_out, and_15_out);
  buf and_15 (and_15_out, _5_2_out);  // AND_Gate
  buf and_16 (and_16_out, _5_2_out);  // AND_Gate
  buf and_17 (and_17_out, _5_2_out);  // AND_Gate
  buf and_18 (and_18_out, _5_2_out);  // AND_Gate
  buf and_19 (and_19_out, _5_2_out);  // AND_Gate
  buf and_20 (and_20_out, _6_2_out);  // AND_Gate
  or or_9 (or_9_out, and_19_out, and_20_out);
  buf and_21 (and_21_out, _6_2_out);  // AND_Gate
  buf and_22 (and_22_out, _6_2_out);  // AND_Gate
  buf and_23 (and_23_out, _6_2_out);  // AND_Gate
  or or_10 (or_10_out, _7_2_out, _8_2_out, _9_2_out, _10_2_out, _11_2_out, _12_2_out);
  and and_24 (and_24_out, and_26_out, _11_2_out);
  and and_25 (and_25_out, and_26_out, _12_2_out);
  or or_11 (or_11_out, and_34_out, and_32_out);
  or or_12 (or_12_out, and_25_out, and_27_out);
  not not_29 (not_29_out, OP_CODE[7]);
  not not_30 (not_30_out, OP_CODE[7]);
  not not_31 (not_31_out, OP_CODE[7]);
  and and_26 (and_26_out, not_30_out, not_29_out, not_31_out);
  and and_27 (and_27_out, _11_2_out, and_26_out);
  and and_28 (and_28_out, _11_2_out, and_26_out);
  and and_29 (and_29_out, and_26_out, _12_2_out);
  and and_30 (and_30_out, and_26_out, _12_2_out, not_32_out);
  or or_13 (or_13_out, and_28_out, or_14_out);
  and and_31 (and_31_out, and_26_out, _7_2_out);
  and and_32 (and_32_out, and_26_out, _7_2_out);
  and and_33 (and_33_out, _8_2_out, and_26_out);
  and and_34 (and_34_out, _8_2_out, and_26_out);
  and and_35 (and_35_out, _9_2_out, and_26_out);
  and and_36 (and_36_out, _11_2_out, and_26_out);
  and and_37 (and_37_out, _11_2_out, and_26_out);
  not not_32 (not_32_out, OP_CODE[7]);
  and and_38 (and_38_out, and_26_out, _12_2_out, OP_CODE[7]);
  and and_39 (and_39_out, and_26_out, _12_2_out, not_32_out);
  and and_40 (and_40_out, and_26_out, _7_2_out);
  and and_41 (and_41_out, _8_2_out, and_26_out);
  and and_42 (and_42_out, _10_2_out, and_26_out);
  or or_14 (or_14_out, and_35_out, and_33_out, and_42_out);
  and and_43 (and_43_out, and_26_out, _12_2_out, OP_CODE[7]);
  not not_33 (not_33_out, OP_CODE[7]);
  not not_34 (not_34_out, OP_CODE[7]);
  and and_44 (and_44_out, not_33_out, not_34_out, OP_CODE[7]);
  or or_15 (or_15_out, _9_2_out, _10_2_out, _11_2_out, _12_2_out);
  and and_45 (and_45_out, and_44_out, or_15_out);
  and and_46 (and_46_out, and_44_out, _7_2_out);
  and and_47 (and_47_out, and_44_out, _8_2_out);
  and and_48 (and_48_out, and_44_out, _9_2_out);
  and and_49 (and_49_out, and_44_out, _10_2_out);
  and and_50 (and_50_out, and_44_out, _11_2_out);
  and and_51 (and_51_out, and_44_out, _12_2_out);
  and and_52 (and_52_out, and_44_out, _7_2_out);
  and and_53 (and_53_out, and_44_out, _7_2_out);
  and and_54 (and_54_out, and_44_out, _8_2_out);
  and and_55 (and_55_out, and_44_out, _8_2_out, OP_CODE[7]);
  and and_56 (and_56_out, and_44_out, _9_2_out);
  and and_57 (and_57_out, and_44_out, _9_2_out);
  and and_58 (and_58_out, and_44_out, _10_2_out);
  and and_59 (and_59_out, and_44_out, _10_2_out);
  not not_35 (not_35_out, OP_CODE[7]);
  and and_60 (and_60_out, and_44_out, _8_2_out, not_35_out);
  and and_61 (and_61_out, and_44_out, _8_2_out);
  not not_36 (not_36_out, OP_CODE[7]);
  and and_62 (and_62_out, not_36_out, OP_CODE[7], not_37_out);
  not not_37 (not_37_out, OP_CODE[7]);
  not not_38 (not_38_out, OP_CODE[7]);
  and and_63 (and_63_out, _7_2_out, and_62_out, OP_CODE[7]);
  and and_64 (and_64_out, _7_2_out, and_62_out, not_38_out);
  not not_39 (not_39_out, OP_CODE[7]);
  and and_65 (and_65_out, OP_CODE[7], and_62_out, _8_2_out);
  and and_66 (and_66_out, not_39_out, and_62_out, _8_2_out);
  and and_67 (and_67_out, and_62_out, _9_2_out);
  and and_68 (and_68_out, and_62_out, _9_2_out);
  and and_69 (and_69_out, STATUS_ZERO_FLAG, and_62_out, _10_2_out);
  and and_70 (and_70_out, STATUS_ZERO_FLAG, and_62_out, _10_2_out);
  and and_71 (and_71_out, and_62_out, _7_2_out);
  and and_72 (and_72_out, and_62_out, _7_2_out);
  and and_73 (and_73_out, and_62_out, _8_2_out);
  and and_74 (and_74_out, and_62_out, _8_2_out);
  and and_75 (and_75_out, and_62_out, _9_2_out);
  and and_76 (and_76_out, and_62_out, _9_2_out);
  and and_77 (and_77_out, and_62_out, _9_2_out);
  not not_40 (not_40_out, OP_CODE[7]);
  and and_78 (and_78_out, not_40_out, OP_CODE[7], OP_CODE[7]);
  not not_41 (not_41_out, STATUS_ZERO_FLAG);
  not not_42 (not_42_out, OP_CODE[7]);
  and and_79 (and_79_out, _7_2_out, and_78_out, OP_CODE[7]);
  and and_80 (and_80_out, _7_2_out, and_78_out, not_42_out);
  not not_43 (not_43_out, OP_CODE[7]);
  and and_81 (and_81_out, OP_CODE[7], and_78_out, _8_2_out);
  and and_82 (and_82_out, not_43_out, and_78_out, _8_2_out);
  and and_83 (and_83_out, and_78_out, _9_2_out);
  and and_84 (and_84_out, and_78_out, _9_2_out);
  and and_85 (and_85_out, not_41_out, and_78_out, _10_2_out);
  and and_86 (and_86_out, not_41_out, and_78_out, _10_2_out);
  and and_87 (and_87_out, and_78_out, _7_2_out);
  and and_88 (and_88_out, and_78_out, _7_2_out);
  and and_89 (and_89_out, and_78_out, _8_2_out);
  and and_90 (and_90_out, and_78_out, _8_2_out);
  and and_91 (and_91_out, and_78_out, _9_2_out);
  and and_92 (and_92_out, and_78_out, _9_2_out);
  and and_93 (and_93_out, and_78_out, _9_2_out);
  not not_44 (not_44_out, OP_CODE[7]);
  not not_45 (not_45_out, OP_CODE[7]);
  and and_94 (and_94_out, OP_CODE[7], not_45_out, not_44_out, not_46_out);
  not not_46 (not_46_out, OP_CODE[7]);
  not not_47 (not_47_out, OP_CODE[7]);
  and and_95 (and_95_out, _7_2_out, and_94_out, OP_CODE[7]);
  and and_96 (and_96_out, _7_2_out, and_94_out, not_47_out);
  not not_48 (not_48_out, OP_CODE[7]);
  and and_97 (and_97_out, not_48_out, and_94_out, _8_2_out);
  and and_98 (and_98_out, OP_CODE[7], and_94_out, _8_2_out);
  and and_99 (and_99_out, and_94_out, _9_2_out);
  and and_100 (and_100_out, and_94_out, _9_2_out);
  not not_49 (not_49_out, OP_CODE[7]);
  and and_101 (and_101_out, and_94_out, _10_2_out);
  and and_102 (and_102_out, and_94_out, _10_2_out, not_49_out);
  and and_103 (and_103_out, and_94_out, _7_2_out);
  and and_104 (and_104_out, and_94_out, _7_2_out);
  and and_105 (and_105_out, and_94_out, _8_2_out);
  and and_106 (and_106_out, and_94_out, _8_2_out);
  and and_107 (and_107_out, and_94_out, _9_2_out);
  and and_108 (and_108_out, and_94_out, _9_2_out);
  not not_50 (not_50_out, OP_CODE[7]);
  and and_109 (and_109_out, and_94_out, _10_2_out, not_50_out);
  and and_110 (and_110_out, and_94_out, _10_2_out, OP_CODE[7]);
  and and_111 (and_111_out, and_94_out, _9_2_out);
  and and_112 (and_112_out, and_94_out, _9_2_out);
  and and_113 (and_113_out, and_94_out, _10_2_out, OP_CODE[7]);
  and and_114 (and_114_out, and_94_out, _9_2_out);
  not not_51 (not_51_out, OP_CODE[7]);
  not not_52 (not_52_out, OP_CODE[7]);
  and and_115 (and_115_out, OP_CODE[7], not_51_out, not_52_out, OP_CODE[7]);
  not not_53 (not_53_out, OP_CODE[7]);
  and and_116 (and_116_out, _7_2_out, and_115_out, not_53_out);
  not not_54 (not_54_out, OP_CODE[7]);
  and and_117 (and_117_out, not_54_out, and_115_out, _8_2_out);
  and and_118 (and_118_out, and_115_out, _9_2_out);
  and and_119 (and_119_out, and_115_out, _9_2_out);
  and and_120 (and_120_out, and_115_out, _10_2_out, not_55_out);
  and and_121 (and_121_out, and_115_out, _10_2_out);
  and and_122 (and_122_out, and_115_out, _7_2_out);
  and and_123 (and_123_out, _7_2_out, and_115_out, OP_CODE[7]);
  and and_124 (and_124_out, and_115_out, _8_2_out);
  and and_125 (and_125_out, OP_CODE[7], and_115_out, _8_2_out);
  and and_126 (and_126_out, and_115_out, _9_2_out);
  and and_127 (and_127_out, and_115_out, _9_2_out);
  not not_55 (not_55_out, OP_CODE[7]);
  not not_56 (not_56_out, OP_CODE[7]);
  and and_128 (and_128_out, and_115_out, _10_2_out, OP_CODE[7]);
  and and_129 (and_129_out, and_115_out, _10_2_out, not_56_out);
  and and_130 (and_130_out, and_115_out, _7_2_out);
  and and_131 (and_131_out, and_115_out, _8_2_out);
  and and_132 (and_132_out, and_115_out, _9_2_out);
  and and_133 (and_133_out, and_115_out, _9_2_out);
  and and_134 (and_134_out, and_115_out, _10_2_out, OP_CODE[7]);
  and and_135 (and_135_out, and_115_out, _9_2_out);
  not not_57 (not_57_out, OP_CODE[7]);
  not not_58 (not_58_out, OP_CODE[7]);
  and and_136 (and_136_out, OP_CODE[7], not_57_out, OP_CODE[7], not_58_out);
  or or_16 (or_16_out, _12_2_out, _11_2_out, _10_2_out, _9_2_out, _8_2_out);
  not not_59 (not_59_out, OP_CODE[7]);
  and and_137 (and_137_out, _7_2_out, and_136_out, not_59_out);
  and and_138 (and_138_out, and_136_out, or_16_out);
  and and_139 (and_139_out, _7_2_out, and_136_out, OP_CODE[7]);
  and and_140 (and_140_out, and_136_out, _7_2_out);
  and and_141 (and_141_out, and_136_out, or_16_out);
  and and_142 (and_142_out, and_136_out, or_16_out);
  and and_143 (and_143_out, and_136_out, _7_2_out);
  and and_144 (and_144_out, and_136_out, _7_2_out);
  not not_60 (not_60_out, OP_CODE[7]);
  and and_145 (and_145_out, OP_CODE[7], not_60_out, OP_CODE[7], OP_CODE[7]);
  and and_146 (and_146_out, _7_2_out, and_145_out);
  and and_147 (and_147_out, _7_2_out, and_145_out);
  not not_61 (not_61_out, OP_CODE[7]);
  not not_62 (not_62_out, OP_CODE[7]);
  and and_148 (and_148_out, and_145_out, _8_2_out, not_62_out);
  and and_149 (and_149_out, and_145_out, _8_2_out, not_61_out);
  and and_150 (and_150_out, _7_2_out, and_145_out);
  and and_151 (and_151_out, _7_2_out, and_145_out);
  and and_152 (and_152_out, and_145_out, _8_2_out, OP_CODE[7]);
  and and_153 (and_153_out, and_145_out, _8_2_out, OP_CODE[7]);
  and and_154 (and_154_out, _7_2_out, and_145_out);
  and and_155 (and_155_out, _8_2_out, and_145_out);
  and and_156 (and_156_out, _8_2_out, and_145_out);
  and and_157 (and_157_out, OP_CODE[7], OP_CODE[7], not_64_out, not_65_out);
  // NOT_Gate not_63 has open pins: in=and_157_out, out=open
  not not_64 (not_64_out, OP_CODE[7]);
  not not_65 (not_65_out, OP_CODE[7]);
  not not_66 (not_66_out, OP_CODE[7]);
  and and_158 (and_158_out, OP_CODE[7], OP_CODE[7], not_66_out, OP_CODE[7]);
  not not_67 (not_67_out, OP_CODE[7]);
  and and_159 (and_159_out, _7_2_out, and_158_out, OP_CODE[7]);
  and and_160 (and_160_out, _7_2_out, and_158_out, not_67_out);
  not not_68 (not_68_out, OP_CODE[7]);
  and and_161 (and_161_out, not_68_out, and_158_out, _8_2_out);
  and and_162 (and_162_out, OP_CODE[7], and_158_out, _8_2_out);
  and and_163 (and_163_out, and_158_out, _9_2_out);
  and and_164 (and_164_out, and_158_out, _9_2_out);
  not not_69 (not_69_out, OP_CODE[7]);
  and and_165 (and_165_out, and_158_out, _10_2_out, not_69_out);
  and and_166 (and_166_out, and_158_out, _10_2_out);
  and and_167 (and_167_out, and_158_out, _7_2_out);
  and and_168 (and_168_out, and_158_out, _7_2_out);
  and and_169 (and_169_out, and_158_out, _8_2_out);
  and and_170 (and_170_out, and_158_out, _8_2_out);
  and and_171 (and_171_out, and_158_out, _9_2_out);
  and and_172 (and_172_out, and_158_out, _9_2_out);
  not not_70 (not_70_out, OP_CODE[7]);
  and and_173 (and_173_out, and_158_out, _10_2_out, OP_CODE[7]);
  and and_174 (and_174_out, and_158_out, _10_2_out, not_70_out);
  and and_175 (and_175_out, and_158_out, _9_2_out);
  and and_176 (and_176_out, and_158_out, _9_2_out);
  and and_177 (and_177_out, and_158_out, _10_2_out, OP_CODE[7]);
  and and_178 (and_178_out, and_158_out, _9_2_out);
  // OR_Gate or_17 has open pins: out=D0_EN
  // OR_Gate or_18 has open pins: out=D0_RW
  // OR_Gate or_19 has open pins: out=D1_EN
  // OR_Gate or_20 has open pins: out=D1_RW
  // OR_Gate or_21 has open pins: out=L_EN
  // OR_Gate or_22 has open pins: out=L_RW
  // OR_Gate or_23 has open pins: out=R_EN
  // OR_Gate or_24 has open pins: out=R_RW
  // OR_Gate or_25 has open pins: out=A_EN
  // OR_Gate or_26 has open pins: out=A_RW
  // OR_Gate or_27 has open pins: out=STATUS_EN
  // OR_Gate or_28 has open pins: out=STATUS_RW
  // OR_Gate or_29 has open pins: out=MBR_EN
  // OR_Gate or_30 has open pins: out=MBR_RW
  // OR_Gate or_31 has open pins: out=MAR_EN
  // OR_Gate or_32 has open pins: out=MAR_RW

  assign OP_CODE[6:0] = {7{OP_CODE[7]}};

  // Notes on the sheet:
  //   INC RW
  //   INC RW
  //   PC RW
  //   INC EN
  //   Stays 0 because we read
  //   MAR EN
  //   MAR RW
  //   INC EN
  //   MAR EN
  //   TICK 3 RAM TICK2
  //   PC EN
  //   PC EN
  //   MAR RW
  //   TICK 1 : PC - MAR
  //   TICK 2 PC <- PC+1 and RAM TICK1
  //   TICK 4 RAM TICK 3
  //   TICK 5 RAM TICK4 (DR -> MBR)
  //   TICK 6 MBR -> INSTR
  //   PC RW
  //   MAR EN
  //   RAM EN
  //   PC RW
  //   PC EN
  //   The first 6 ticks are for the fetch portion of the CPU
  //   From PC
  //   SYS FROM MAR
  //   FROM PC
  //   INC EN
  //   SYS From MAR
  //   RAM OP
  //   Load
  //   AFAIK, TICK 3-4 only requires RAM EN, everything else happens inside RAM CU
  //   RAM EN
  //   RAM EN
  //   RAM EN
  //   SYS FROM DR
  //   RAM EN
  //   SYS FROM DR
  //   fROM SYS TO MBR
  //   SYS FROM MBR
  //   MBR RW
  //   MBR EN
  //   MBR EN
  //   MBR EN
  //   MBR RW
  //   TO INSTR
  //   INSTR EN
  //   INSTR EN
  //   TO INSTR
  //   FETCH INSTR
  //   INSTR RW
  //   INSTR RW
  //   EXECUTE INSTR
  //   INSTR EN
  //   Load
  //   FROM SYS TO MBR
  //   MBR EN
  //   MBR EN
  //   MAR EN
  //   TICK3
  //   RAM EN
  //   MBR EN
  //   D0 EN
  //   FROM MBR
  //   RAM EN
  //   D0 EN
  //   FROM MBR
  //   D0/D1
  //   LOAD
  //   MAR EN
  //   MAR RW
  //   MAR EN
  //   RAM EN
  //   RAM EN
  //   MBR RW
  //   D1 EN
  //   D0 RW
  //   D1 RW
  //   D1 EN
  //   D0 RW
  //   TICK 1
  //   MAR FROM INSTR
  //   TICK2
  //   SYS FROM MAR
  //   TICK4
  //   RAM EN
  //   TICK5
  //   SYS FROM DR
  //   D1 RW
  //   FROM SYS TO MBR
  //   MBR RW
  //   TICK6
  //   MAR RW
  //   SYS FROM DR
  //   SYS FROM MAR
  //   MAR FROM INSTR
  //   D0/D1
  //   RAM STORE
  //   STORE
  //   MAR EN
  //   MBR EN
  //   MAR EN
  //   MBR EN
  //   RAM EN
  //   RAM EN
  //   ADDRES INTO MAR
  //   REGISTER INTO MBR
  //   4 TICK STORE RAM
  //   MAR FROM INSTR
  //   MAR RW
  //   D1 EN
  //   MBR RW
  //   RAM EN
  //   RAM EN
  //   TICK 5
  //   TICK 6
  //   TICK 1
  //   TO MBR
  //   D0 EN
  //   TICK 3
  //   SYS FROM MAR
  //   TICK 4
  //   SYS FROM MBR
  //   TICK 2
  //   WAIT 2 TICK
  //   BEQ
  //   REG1 - L
  //   REG2 -R
  //   R-L
  //   D0 EN
  //   D1 EN
  //   D0 EN
  //   D1 EN
  //   SUB
  //   L EN
  //   PC EN
  //   PC RW
  //   CHECK STATUS REG FOR ZERO
  //   L RW
  //   L EN
  //   R RW
  //   R EN
  //   STATUS RW
  //   STATUS EN
  //   FROM INSTR
  //   R EN
  //   IS DEFAULT (FROM PC = 0)
  //   WAIT 2 TICK
  //   BNQ
  //   REG1 - L
  //   REG2 -R
  //   R-L
  //   D0 EN
  //   D1 EN
  //   D0 EN
  //   D1 EN
  //   SUB
  //   L EN
  //   PC EN
  //   PC RW
  //   CHECK STATUS REG FOR ZERO
  //   L RW
  //   L EN
  //   R EN
  //   R RW
  //   STATUS RW
  //   STATUS EN
  //   FROM INSTR
  //   R EN
  //   IS DEFAULT (FROM PC = 0)
  //   WAIT 2 TICK
  //   ADD
  //   REG1 - L
  //   REG2 -R
  //   R+L
  //   A REG1
  //   D0 EN
  //   D1 EN
  //   D0 EN
  //   D1 EN
  //   ADD
  //   L EN
  //   A EN
  //   D0 EN
  //   L RW
  //   L EN
  //   R EN
  //   R RW
  //   A  RW
  //   A EN
  //   D1 EN
  //   D0 RW
  //   STAT EN
  //   R EN
  //   D1 RW
  //   STAT RW
  //   WAIT 2 TICK
  //   SUB
  //   REG1 - L
  //   REG2 -R
  //   R-L
  //   A REG1
  //   D0 EN
  //   D0 EN
  //   SUB
  //   L EN
  //   A EN
  //   D0 EN
  //   R RW
  //   D1 EN
  //   R EN
  //   D1 EN
  //   L RW
  //   A  RW
  //   A EN
  //   D1 EN
  //   D0 RW
  //   L EN
  //   STAT EN
  //   R EN
  //   D1 RW
  //   STAT RW
  //   WAIT 4 TICK
  //   PRINT
  //   REG MBR
  //   MBR PRINT
  //   WAIT 4 TICK
  //   D0 EN
  //   MBR EN
  //   PRINT WILL STAY OPEN FOR A TOTAL OF 5 TICKS
  //   MBR EN
  //   D1 EN
  //   SYS FROM MBR
  //   PRINT EN
  //   TO MBR
  //   MBR RW
  //   WAIT 4 TICK
  //   D0 EN
  //   INPUT
  //   INPUT - MBR
  //   MBR REG
  //   WAIT 4 TICK
  //   KEY EN
  //   SYS FROM KEY
  //   DO RW
  //   SYS TO MBR
  //   MBR EN
  //   MBR EN
  //   D1 EN
  //   D1 RW
  //   MBR RW
  //   TO MBR
  //   STOP
  //   SEND TO A GATE WHERE THE CLOCK IS
  //   WHEN STOP IS IN THE INSTR REG, PROGRAM SHOULD STOP
  //   WHEN STOP IS NOT ON, CLOCK TICKS, ELSE CLOCK STOPS
  //   WAIT 2 TICK
  //   MULT
  //   REG1 - L
  //   REG2 -R
  //   R*L
  //   A REG1
  //   D0 EN
  //   D1 EN
  //   D0 EN
  //   D1 EN
  //   MULT
  //   L EN
  //   A EN
  //   D0 EN
  //   L RW
  //   L EN
  //   R RW
  //   R EN
  //   A  RW
  //   A EN
  //   D1 EN
  //   D0 RW
  //   STAT EN
  //   R EN
  //   D1 RW
  //   STAT RW
endmodule

module _4_or_3_bits (
  input  [7:0] in_1,
  output [7:0] out_2,
  output [7:0] out_3
);

  wire and_1_out, and_2_out, and_8_out, and_9_out, and_10_out, and_11_out, and_12_out, and_13_out,
       and_14_out, and_15_out, not_1_out, not_2_out, not_3_out, not_4_out;

  and and_1 (and_1_out, in_1[6], in_1[7]);
  and and_2 (and_2_out, in_1[5], in_1[7]);
  and and_3 (out_2[4], in_1[4], in_1[7]);
  and and_4 (out_2[3], in_1[3], in_1[7]);
  and and_5 (out_2[2], in_1[2], in_1[7]);
  and and_6 (out_2[1], in_1[1], in_1[7]);
  and and_7 (out_2[0], in_1[0], in_1[7]);
  not not_1 (not_1_out, in_1[7]);
  and and_8 (and_8_out, in_1[6], not_1_out);
  and and_9 (and_9_out, in_1[5], not_1_out);
  and and_10 (and_10_out, in_1[4], not_1_out);
  and and_11 (and_11_out, in_1[3], not_1_out);
  and and_12 (and_12_out, in_1[2], not_1_out);
  and and_13 (and_13_out, in_1[1], not_1_out);
  and and_14 (and_14_out, in_1[0], not_1_out);
  not not_2 (not_2_out, in_1[7]);
  not not_3 (not_3_out, and_1_out);
  not not_4 (not_4_out, and_2_out);
  and and_15 (and_15_out, not_2_out, not_4_out);
  or or_1 (out_3[7], 1'b0, in_1[7]);
  or or_2 (out_3[6], and_8_out, in_1[7]);
  or or_3 (out_3[5], and_9_out, in_1[7]);
  or or_4 (out_3[4], and_10_out, 1'b0);
  or or_5 (out_3[3], and_11_out, 1'b0);
  or or_6 (out_3[2], and_12_out, 1'b0);
  or or_7 (out_3[1], and_13_out, 1'b0);
  or or_8 (out_3[0], and_14_out, 1'b0);
  or or_9 (out_2[7], and_15_out, in_1[7]);
  or or_10 (out_2[6], and_15_out, and_1_out);
  or or_11 (out_2[5], and_15_out, and_2_out);
endmodule
